// Logisim project trabalho.circ as structural Verilog: 15 circuits, main circuit main
module main (
  input  in_1,
  input  in_2,
  input  in_3,
  input  in_4,
  input  in_5,
  input  in_6,
  input  in_7,
  input  in_8,
  input  in_9
);

  wire l_d_7ebe929a_1_out_2, l_d_7ebe929a_1_out_3, l_d_7ebe929a_1_out_4, mostrador_1_out_5,
       mostrador_1_out_6, mostrador_1_out_7, mostrador_1_out_8, mostrador_1_out_9, mostrador_1_out_10,
       mostrador_1_out_11, mostrador_2_out_5, mostrador_2_out_6, mostrador_2_out_7, mostrador_2_out_8,
       mostrador_2_out_9, mostrador_2_out_10, mostrador_2_out_11, not_1_out;
  wire [3:0] com_bot_o_7b0cf85d_1_out_4;

  Mostrador mostrador_1 (
    .in_1(in_2), .in_2(in_3), .in_3(in_4), .in_4(in_5), .out_9(mostrador_1_out_9),
    .out_10(mostrador_1_out_10), .out_11(mostrador_1_out_11), .out_5(mostrador_1_out_5),
    .out_6(mostrador_1_out_6), .out_7(mostrador_1_out_7), .out_8(mostrador_1_out_8));
  Mostrador mostrador_2 (
    .in_1(in_6), .in_2(in_7), .in_3(in_8), .in_4(in_9), .out_9(mostrador_2_out_9),
    .out_10(mostrador_2_out_10), .out_11(mostrador_2_out_11), .out_5(mostrador_2_out_5),
    .out_6(mostrador_2_out_6), .out_7(mostrador_2_out_7), .out_8(mostrador_2_out_8));
  _7_Segment_Display u_7_segment_display_1 (
    .g(mostrador_1_out_5), .f(mostrador_1_out_6), .a(mostrador_1_out_7), .b(mostrador_1_out_8),
    .e(mostrador_1_out_9), .d(mostrador_1_out_10), .c(mostrador_1_out_11), .dp(in_1));
  _7_Segment_Display u_7_segment_display_2 (
    .g(mostrador_2_out_5), .f(mostrador_2_out_6), .a(mostrador_2_out_7), .b(mostrador_2_out_8),
    .e(mostrador_2_out_9), .d(mostrador_2_out_10), .c(mostrador_2_out_11), .dp(not_1_out));
  com_bot_o_7b0cf85d com_bot_o_7b0cf85d_1 (
    .in_2({in_6, in_7, in_8, in_9}), .in_3({in_2, in_3, in_4, in_5}), .in_1(in_1),
    .out_4(com_bot_o_7b0cf85d_1_out_4));
  not not_1 (not_1_out, in_1);
  L_d_7ebe929a l_d_7ebe929a_1 (
    .in_1(com_bot_o_7b0cf85d_1_out_4), .out_2(l_d_7ebe929a_1_out_2), .out_3(l_d_7ebe929a_1_out_3),
    .out_4(l_d_7ebe929a_1_out_4));
  LED igual (.in(l_d_7ebe929a_1_out_2));
  LED mais (.in(l_d_7ebe929a_1_out_3));
  LED menos (.in(l_d_7ebe929a_1_out_4));
endmodule

module com_bot_o_7b0cf85d (
  input  in_1,
  input  [3:0] in_2,
  input  [3:0] in_3,
  output [3:0] out_4
);

  triangulo triangulo_1 (.in_2(in_2[0]), .in_3(in_3[0]), .in_1(in_1), .out_4(out_4[0]));
  triangulo triangulo_2 (.in_2(in_2[1]), .in_3(in_3[1]), .in_1(in_1), .out_4(out_4[1]));
  triangulo triangulo_3 (.in_2(in_2[2]), .in_3(in_3[2]), .in_1(in_1), .out_4(out_4[2]));
  triangulo triangulo_4 (.in_2(in_2[3]), .in_3(in_3[3]), .in_1(in_1), .out_4(out_4[3]));
endmodule

module triangulo (
  input  in_1,
  input  in_2,
  input  in_3,
  output out_4
);

  wire and_1_out, and_2_out, and_3_out, and_4_out, not_1_out, not_2_out, not_3_out, not_4_out;

  not not_1 (not_1_out, in_1);
  and and_1 (and_1_out, in_1, in_3, not_2_out);
  not not_2 (not_2_out, in_2);
  and and_2 (and_2_out, not_1_out, in_2, not_3_out);
  not not_3 (not_3_out, in_3);
  not not_4 (not_4_out, in_1);
  and and_3 (and_3_out, not_4_out, in_2, in_3);
  and and_4 (and_4_out, in_1, in_2, in_3);
  or or_1 (out_4, and_1_out, and_2_out, and_3_out, and_4_out);
endmodule

module L_6af18fe5 (
  input  in_1,
  input  in_2,
  input  in_3,
  output out_4
);

  wire and_1_out, and_2_out, not_1_out, not_2_out, not_3_out, not_4_out, or_1_out;

  not not_1 (not_1_out, in_2);
  not not_2 (not_2_out, in_3);
  and and_1 (and_1_out, not_1_out, not_2_out);
  and and_2 (and_2_out, in_2, in_3);
  or or_1 (or_1_out, and_2_out, and_1_out, and_1_out, and_1_out);
  not not_3 (not_3_out, or_1_out);
  not not_4 (not_4_out, in_1);
  and and_3 (out_4, not_3_out, not_4_out);
endmodule

module L_d_7ebe929a (
  input  [3:0] in_1,
  output out_2,
  output out_3,
  output out_4
);

  wire l_00_ou_11_2cab960a_1_out_3, l_00_ou_11_2cab960a_2_out_3, l_00_ou_11_2cab960a_3_out_3,
       l_00_ou_11_2cab960a_4_out_3, L_3e218025_2_out, L_3e218025_3_out, L_3e218025_4_out, L_3e218025_out,
       l_6af18fe5_1_out_4, l_6af18fe5_2_out_4, l_6af18fe5_3_out_4, l_6af18fe5_4_out_4, l_19270569_1_out_3,
       l_19270569_1_out_4, l_19270569_2_out_3, l_19270569_2_out_4, l_19270569_3_out_3, l_19270569_3_out_4,
       l_19270569_4_out_3, l_19270569_4_out_4, L_bb417b61_2_out, L_bb417b61_3_out, L_bb417b61_4_out,
       L_bb417b61_out, mine_2_out, mine_out, mostrador_1_out_5, mostrador_1_out_6, mostrador_1_out_7,
       mostrador_1_out_8, mostrador_1_out_9, mostrador_1_out_10, mostrador_1_out_11;
  wire [3:0] random_1_out;

  Random #(.width(4), .seed(42)) random_1 (.out(random_1_out));  // open: clk, next, clr
  _7_Segment_Display u_7_segment_display_1 (
    .g(mostrador_1_out_8), .f(mostrador_1_out_7), .a(mostrador_1_out_6), .b(mostrador_1_out_5),
    .e(mostrador_1_out_11), .d(mostrador_1_out_10), .c(mostrador_1_out_9));  // open: dp
  Mostrador mostrador_1 (
    .in_1(random_1_out[3]), .in_2(random_1_out[2]), .in_3(random_1_out[1]), .in_4(random_1_out[0]),
    .out_9(mostrador_1_out_9), .out_10(mostrador_1_out_10), .out_11(mostrador_1_out_11),
    .out_5(mostrador_1_out_5), .out_6(mostrador_1_out_6), .out_7(mostrador_1_out_7), .out_8(mostrador_1_out_8));
  L_19270569 l_19270569_1 (
    .in_1(in_1[2]), .in_2(random_1_out[2]), .out_3(l_19270569_1_out_3), .out_4(l_19270569_1_out_4));
  L_19270569 l_19270569_2 (
    .in_1(in_1[0]), .in_2(random_1_out[0]), .out_3(l_19270569_2_out_3), .out_4(l_19270569_2_out_4));
  L_00_ou_11_2cab960a l_00_ou_11_2cab960a_1 (
    .in_1(in_1[0]), .in_2(random_1_out[0]), .out_3(l_00_ou_11_2cab960a_1_out_3));
  L_00_ou_11_2cab960a l_00_ou_11_2cab960a_2 (
    .in_1(random_1_out[1]), .in_2(in_1[1]), .out_3(l_00_ou_11_2cab960a_2_out_3));
  L_00_ou_11_2cab960a l_00_ou_11_2cab960a_3 (
    .in_1(in_1[2]), .in_2(random_1_out[2]), .out_3(l_00_ou_11_2cab960a_3_out_3));
  L_00_ou_11_2cab960a l_00_ou_11_2cab960a_4 (
    .in_1(in_1[3]), .in_2(random_1_out[3]), .out_3(l_00_ou_11_2cab960a_4_out_3));
  L_19270569 l_19270569_3 (
    .in_1(in_1[3]), .in_2(random_1_out[3]), .out_3(l_19270569_3_out_3), .out_4(l_19270569_3_out_4));
  L_19270569 l_19270569_4 (
    .in_1(in_1[1]), .in_2(random_1_out[1]), .out_3(l_19270569_4_out_3), .out_4(l_19270569_4_out_4));
  and and_1 (out_2, l_00_ou_11_2cab960a_1_out_3, l_00_ou_11_2cab960a_2_out_3, l_00_ou_11_2cab960a_3_out_3, l_00_ou_11_2cab960a_4_out_3);
  L_6af18fe5 l_6af18fe5_1 (
    .in_2(l_19270569_3_out_3), .in_3(l_19270569_3_out_4), .in_1(out_2), .out_4(l_6af18fe5_1_out_4));
  L_6af18fe5 l_6af18fe5_2 (
    .in_2(l_19270569_1_out_3), .in_3(l_19270569_1_out_4), .in_1(l_6af18fe5_1_out_4),
    .out_4(l_6af18fe5_2_out_4));
  or mine (mine_out, l_6af18fe5_1_out_4, l_6af18fe5_2_out_4);
  or mine_2 (mine_2_out, mine_out, l_6af18fe5_3_out_4);
  L_6af18fe5 l_6af18fe5_3 (
    .in_2(l_19270569_4_out_3), .in_3(l_19270569_4_out_4), .in_1(mine_out), .out_4(l_6af18fe5_3_out_4));
  L_6af18fe5 l_6af18fe5_4 (
    .in_2(l_19270569_2_out_3), .in_3(l_19270569_2_out_4), .in_1(mine_2_out), .out_4(l_6af18fe5_4_out_4));
  and L_3e218025 (L_3e218025_out, l_19270569_3_out_3, l_6af18fe5_1_out_4);
  and L_bb417b61 (L_bb417b61_out, l_6af18fe5_1_out_4, l_19270569_3_out_4);
  and L_3e218025_2 (L_3e218025_2_out, l_19270569_1_out_3, l_6af18fe5_2_out_4);
  and L_bb417b61_2 (L_bb417b61_2_out, l_6af18fe5_2_out_4, l_19270569_1_out_4);
  and L_3e218025_3 (L_3e218025_3_out, l_19270569_4_out_3, l_6af18fe5_3_out_4);
  and L_bb417b61_3 (L_bb417b61_3_out, l_6af18fe5_3_out_4, l_19270569_4_out_4);
  and L_3e218025_4 (L_3e218025_4_out, l_19270569_2_out_3, l_6af18fe5_4_out_4);
  and L_bb417b61_4 (L_bb417b61_4_out, l_6af18fe5_4_out_4, l_19270569_2_out_4);
  or L_3e218025_5 (out_3, L_3e218025_out, L_3e218025_2_out, L_3e218025_3_out, L_3e218025_4_out);
  or L_bb417b61_5 (out_4, L_bb417b61_out, L_bb417b61_2_out, L_bb417b61_3_out, L_bb417b61_4_out);
endmodule

module L_19270569 (
  input  in_1,
  input  in_2,
  output out_3,
  output out_4
);

  wire not_1_out, not_2_out;

  not not_1 (not_1_out, in_2);
  not not_2 (not_2_out, in_1);
  and L_3e218025 (out_3, in_1, not_1_out);
  and L_bb417b61 (out_4, not_2_out, in_2);
endmodule

module L_00_ou_11_2cab960a (
  input  in_1,
  input  in_2,
  output out_3
);

  wire and_1_out, and_2_out, not_1_out, not_2_out;

  not not_1 (not_1_out, in_1);
  not not_2 (not_2_out, in_2);
  and and_1 (and_1_out, not_1_out, not_2_out);
  and and_2 (and_2_out, in_1, in_2);
  or or_1 (out_3, and_1_out, and_2_out);
endmodule

module Seg_Piso (
  input  A,
  input  B,
  input  C,
  input  D,
  output out_5
);

  wire and_1_out, and_2_out, and_3_out, and_4_out, and_5_out, and_6_out, not_1_out, not_2_out, not_3_out,
       not_4_out;

  not not_1 (not_1_out, A);
  not not_2 (not_2_out, B);
  not not_3 (not_3_out, C);
  not not_4 (not_4_out, D);
  and and_1 (and_1_out, A, B, not_3_out);
  and and_2 (and_2_out, not_1_out, not_2_out, C);
  and and_3 (and_3_out, B, not_3_out, D);
  and and_4 (and_4_out, not_2_out, not_3_out, not_4_out);
  and and_5 (and_5_out, B, C, not_4_out);
  and and_6 (and_6_out, A, not_2_out, D);
  or or_1 (out_5, and_1_out, and_2_out, and_3_out, and_4_out, and_5_out, and_6_out);
endmodule

module Seg_Teto (
  input  A,
  input  B,
  input  C,
  input  D,
  output out_5
);

  wire and_1_out, and_2_out, and_3_out, and_4_out, and_5_out, and_6_out, and_7_out, not_1_out, not_2_out,
       not_3_out, not_4_out;

  not not_1 (not_1_out, A);
  not not_2 (not_2_out, B);
  not not_3 (not_3_out, C);
  not not_4 (not_4_out, D);
  and and_1 (and_1_out, D, C, B);
  and and_2 (and_2_out, D, not_1_out, C);
  and and_3 (and_3_out, not_1_out, not_2_out, not_4_out);
  and and_4 (and_4_out, A, not_3_out, not_4_out);
  and and_5 (and_5_out, not_4_out, C);
  and and_6 (and_6_out, not_2_out, not_3_out, A);
  and and_7 (and_7_out, not_1_out, B, D);
  or or_1 (out_5, and_1_out, and_2_out, and_3_out, and_4_out, and_5_out, and_6_out, and_7_out);
endmodule

module Seg_Meio (
  input  A,
  input  B,
  input  C,
  input  D,
  output out_5
);

  wire and_1_out, and_2_out, and_3_out, and_4_out, and_5_out, not_1_out, not_2_out, not_3_out, not_4_out;

  not not_1 (not_1_out, A);
  not not_2 (not_2_out, B);
  not not_3 (not_3_out, C);
  not not_4 (not_4_out, D);
  and and_1 (and_1_out, A, not_2_out);
  and and_2 (and_2_out, not_3_out, B, not_1_out);
  and and_3 (and_3_out, not_1_out, not_2_out, C);
  and and_4 (and_4_out, C, not_4_out);
  and and_5 (and_5_out, A, B, D);
  or or_1 (out_5, and_1_out, and_2_out, and_3_out, and_4_out, and_5_out);
endmodule

module Seg_Dir_Baixo (
  input  A,
  input  B,
  input  C,
  input  D,
  output out_5
);

  wire and_1_out, and_2_out, and_3_out, and_4_out, and_5_out, not_1_out, not_2_out, not_3_out;

  not not_1 (not_1_out, A);
  not not_2 (not_2_out, B);
  not not_3 (not_3_out, C);
  and and_1 (and_1_out, not_1_out, B);
  and and_2 (and_2_out, not_1_out, not_2_out, not_3_out);
  and and_3 (and_3_out, not_2_out, A);
  and and_4 (and_4_out, not_3_out, D);
  and and_5 (and_5_out, not_1_out, C, D);
  or or_1 (out_5, and_1_out, and_2_out, and_3_out, and_4_out, and_5_out);
endmodule

module Seg_Esq_Baixo (
  input  A,
  input  B,
  input  C,
  input  D,
  output out_5
);

  wire and_1_out, and_2_out, and_3_out, and_4_out, not_2_out, not_3_out, not_4_out;

  // NOT_Gate not_1 has open pins: in=A, out=open
  not not_2 (not_2_out, B);
  not not_3 (not_3_out, C);
  not not_4 (not_4_out, D);
  and and_1 (and_1_out, A, not_2_out, C);
  and and_2 (and_2_out, A, B);
  and and_3 (and_3_out, not_2_out, not_3_out, not_4_out);
  and and_4 (and_4_out, C, not_4_out);
  or or_1 (out_5, and_1_out, and_2_out, and_3_out, and_4_out);
endmodule

module Seg_Dir_Cima (
  input  A,
  input  B,
  input  C,
  input  D,
  output out_5
);

  wire and_1_out, and_2_out, and_3_out, and_4_out, and_5_out, not_1_out, not_2_out, not_3_out, not_4_out;

  not not_1 (not_1_out, A);
  not not_2 (not_2_out, B);
  not not_3 (not_3_out, C);
  not not_4 (not_4_out, D);
  and and_1 (and_1_out, D, A, not_3_out);
  and and_2 (and_2_out, not_1_out, not_2_out);
  and and_3 (and_3_out, not_2_out, A, not_4_out);
  and and_4 (and_4_out, not_4_out, not_3_out, not_1_out);
  and and_5 (and_5_out, not_1_out, C, D);
  or or_1 (out_5, and_1_out, and_2_out, and_3_out, and_4_out, and_5_out);
endmodule

module Seg_Esq_Cima (
  input  A,
  input  B,
  input  C,
  input  D,
  output out_5
);

  wire and_1_out, and_2_out, and_3_out, and_4_out, and_5_out, not_1_out, not_2_out, not_3_out, not_4_out;

  not not_1 (not_1_out, A);
  not not_2 (not_2_out, B);
  not not_3 (not_3_out, C);
  not not_4 (not_4_out, D);
  and and_1 (and_1_out, A, not_2_out);
  and and_2 (and_2_out, not_1_out, B, not_3_out);
  and and_3 (and_3_out, B, not_4_out, C);
  and and_4 (and_4_out, not_3_out, not_4_out);
  and and_5 (and_5_out, A, B, C);
  or or_1 (out_5, and_1_out, and_2_out, and_3_out, and_4_out, and_5_out);
endmodule

module Mostrador (
  input  in_1,
  input  in_2,
  input  in_3,
  input  in_4,
  output out_5,
  output out_6,
  output out_7,
  output out_8,
  output out_9,
  output out_10,
  output out_11
);

  Seg_Meio seg_meio_1 (.A(in_1), .B(in_2), .C(in_3), .D(in_4), .out_5(out_5));
  Seg_Esq_Cima seg_esq_cima_1 (.A(in_1), .B(in_2), .C(in_3), .D(in_4), .out_5(out_6));
  Seg_Dir_Cima seg_dir_cima_1 (.A(in_1), .B(in_2), .C(in_3), .D(in_4), .out_5(out_8));
  Seg_Teto seg_teto_1 (.A(in_1), .B(in_2), .C(in_3), .D(in_4), .out_5(out_7));
  Seg_Dir_Baixo seg_dir_baixo_1 (.A(in_1), .B(in_2), .C(in_3), .D(in_4), .out_5(out_11));
  Seg_Piso seg_piso_1 (.A(in_1), .B(in_2), .C(in_3), .D(in_4), .out_5(out_10));
  Seg_Esq_Baixo seg_esq_baixo_1 (.A(in_1), .B(in_2), .C(in_3), .D(in_4), .out_5(out_9));
endmodule
