// Logisim project trabalho2.7.circ as structural Verilog: 30 circuits, main circuit main
module com_bot_o_7b0cf85d (
  input  in_1,
  input  [3:0] in_2,
  input  [3:0] in_3,
  output [3:0] out_4
);

  wire not_1_out, not_2_out, not_3_out, not_4_out;

  not not_1 (not_1_out, in_1);
  not not_2 (not_2_out, not_1_out);
  not not_3 (not_3_out, not_2_out);
  not not_4 (not_4_out, not_3_out);
  triangulo triangulo_1 (.in_2(in_2[0]), .in_3(in_3[0]), .in_1(not_4_out), .out_4(out_4[0]));
  triangulo triangulo_2 (.in_2(in_2[1]), .in_3(in_3[1]), .in_1(not_4_out), .out_4(out_4[1]));
  triangulo triangulo_3 (.in_2(in_2[2]), .in_3(in_3[2]), .in_1(not_4_out), .out_4(out_4[2]));
  triangulo triangulo_4 (.in_2(in_2[3]), .in_3(in_3[3]), .in_1(not_4_out), .out_4(out_4[3]));
endmodule

module main (
  output out_1
);

  wire alavan_1_out_2, and_1_out, button_1_out, button_2_out, button_3_out, button_4_out, button_5_out,
       c6_out_3, c9_2_out_3, c9_3_out_3, clock_1_out, or_1_out, or_2_out, or_3_out, or_4_out, relogio_9_1__0,
       relogio_9_1__9, relogio_9_2__9, relojo6_1__0, relojo6_1__6, rlogio_9_esp_1_out_5,
       rlogio_9_esp_1_out_6, xor_1_out, xor_2_out, xor_3_out;
  wire [3:0] c6_out_2, c9_2_out_2, c9_3_out_2, c9_out_2, relogio_9_1_sai, relogio_9_2_sai, relojo6_1_out_6,
       rlogio_9_esp_1_sai;

  xor xor_1 (xor_1_out, button_1_out, c9_2_out_3);
  cot_9 c9 (.clk(xor_1_out), .out_2(c9_out_2));  // open: out_3
  Hex_Digit_Display hex_digit_display_1 (.value(c9_out_2));  // open: dp
  or or_1 (or_1_out, relogio_9_1__9, and_1_out);
  rlogio_9_esp rlogio_9_esp_1 (
    .clk(or_1_out), .out_5(rlogio_9_esp_1_out_5), .\config (alavan_1_out_2), .out_6(rlogio_9_esp_1_out_6),
    .sai(rlogio_9_esp_1_sai), .usu(c9_out_2));
  Hex_Digit_Display hex_digit_display_2 (.value(rlogio_9_esp_1_sai));  // open: dp
  cot_9 c9_2 (.clk(xor_2_out), .out_2(c9_2_out_2), .out_3(c9_2_out_3));
  Button button_1 (.out(button_1_out));
  Hex_Digit_Display hex_digit_display_3 (.value(c9_2_out_2));  // open: dp
  or or_2 (or_2_out, and_1_out, relojo6_1__6);
  Hex_Digit_Display hex_digit_display_4 (.value(relogio_9_1_sai));  // open: dp
  xor xor_2 (xor_2_out, button_2_out, c6_out_3);
  cot_6 c6 (.clk(xor_3_out), .out_2(c6_out_2), .out_3(c6_out_3));
  Button button_2 (.out(button_2_out));
  Hex_Digit_Display hex_digit_display_5 (.value(c6_out_2));  // open: dp
  or or_3 (or_3_out, relogio_9_2__9, and_1_out);
  relogio_9 relogio_9_1 (
    .clk(or_2_out), .in_3(rlogio_9_esp_1_out_6), .in_4(rlogio_9_esp_1_out_5), .sai(relogio_9_1_sai),
    ._0(relogio_9_1__0), .usu(c9_2_out_2), .\config (alavan_1_out_2), ._9(relogio_9_1__9));  // open: de_f
  Hex_Digit_Display hex_digit_display_6 (.value(relojo6_1_out_6));  // open: dp
  xor xor_3 (xor_3_out, button_3_out, c9_3_out_3);
  Button button_3 (.out(button_3_out));
  Hex_Digit_Display hex_digit_display_7 (.value(c9_3_out_2));  // open: dp
  or or_4 (or_4_out, clock_1_out, and_1_out);
  relojo6 relojo6_1 (
    .clk(or_3_out), .f_18(relogio_9_1__0), .in_3(rlogio_9_esp_1_out_6), .\config (alavan_1_out_2),
    ._6(relojo6_1__6), .out_6(relojo6_1_out_6), .usu(c6_out_2), ._0(relojo6_1__0));
  TTTTT ttttt_1 (
    .in_1(rlogio_9_esp_1_sai), .in_2(relogio_9_1_sai), .in_3(relojo6_1_out_6), .in_4(relogio_9_2_sai),
    .out_5(out_1));
  Button button_4 (.out(button_4_out));
  cot_9 c9_3 (.clk(button_4_out), .out_2(c9_3_out_2), .out_3(c9_3_out_3));
  relogio_9 relogio_9_2 (
    .clk(or_4_out), .de_f(relojo6_1__0), .in_3(relogio_9_1__0), .in_4(rlogio_9_esp_1_out_6),
    .sai(relogio_9_2_sai), .usu(c9_3_out_2), .\config (alavan_1_out_2), ._9(relogio_9_2__9));  // open: _0
  and and_1 (and_1_out, clock_1_out, alavan_1_out_2);
  Hex_Digit_Display hex_digit_display_8 (.value(relogio_9_2_sai));  // open: dp
  Clock clock_1 (.out(clock_1_out));
  alavan alavan_1 (.in_1(button_5_out), .out_2(alavan_1_out_2));
  Button button_5 (.out(button_5_out));
endmodule

module triangulo (
  input  in_1,
  input  in_2,
  input  in_3,
  output out_4
);

  wire and_1_out, and_2_out, and_3_out, and_4_out, not_1_out, not_2_out, not_3_out, not_4_out;

  not not_1 (not_1_out, in_1);
  and and_1 (and_1_out, in_1, in_3, not_2_out);
  not not_2 (not_2_out, in_2);
  and and_2 (and_2_out, not_1_out, in_2, not_3_out);
  not not_3 (not_3_out, in_3);
  not not_4 (not_4_out, in_1);
  and and_3 (and_3_out, not_4_out, in_2, in_3);
  and and_4 (and_4_out, in_1, in_2, in_3);
  or or_1 (out_4, and_1_out, and_2_out, and_3_out, and_4_out);
endmodule

module L_6af18fe5 (
  input  in_1,
  input  in_2,
  input  in_3,
  output out_4
);

  wire and_1_out, and_2_out, not_1_out, not_2_out, not_3_out, not_4_out, or_1_out;

  not not_1 (not_1_out, in_2);
  not not_2 (not_2_out, in_3);
  and and_1 (and_1_out, not_1_out, not_2_out);
  and and_2 (and_2_out, in_2, in_3);
  or or_1 (or_1_out, and_2_out, and_1_out, and_1_out, and_1_out);
  not not_3 (not_3_out, or_1_out);
  not not_4 (not_4_out, in_1);
  and and_3 (out_4, not_3_out, not_4_out);
endmodule

module L_d_7ebe929a (
  input  [3:0] in_1,
  output out_2,
  output out_3,
  output out_4
);

  wire l_00_ou_11_2cab960a_1_out_3, l_00_ou_11_2cab960a_2_out_3, l_00_ou_11_2cab960a_3_out_3,
       l_00_ou_11_2cab960a_4_out_3, L_3e218025_2_out, L_3e218025_3_out, L_3e218025_4_out, L_3e218025_out,
       l_6af18fe5_1_out_4, l_6af18fe5_2_out_4, l_6af18fe5_3_out_4, l_6af18fe5_4_out_4, l_19270569_1_out_3,
       l_19270569_1_out_4, l_19270569_2_out_3, l_19270569_2_out_4, l_19270569_3_out_3, l_19270569_3_out_4,
       l_19270569_4_out_3, l_19270569_4_out_4, L_bb417b61_2_out, L_bb417b61_3_out, L_bb417b61_4_out,
       L_bb417b61_out, mine_2_out, mine_out, mostrador_1_out_5, mostrador_1_out_6, mostrador_1_out_7,
       mostrador_1_out_8, mostrador_1_out_9, mostrador_1_out_10, mostrador_1_out_11;
  wire [3:0] random_1_out;

  Random #(.width(4), .seed(42)) random_1 (.out(random_1_out));  // open: clk, next, clr
  _7_Segment_Display u_7_segment_display_1 (
    .g(mostrador_1_out_8), .f(mostrador_1_out_7), .a(mostrador_1_out_6), .b(mostrador_1_out_5),
    .e(mostrador_1_out_11), .d(mostrador_1_out_10), .c(mostrador_1_out_9));  // open: dp
  Mostrador mostrador_1 (
    .in_1(random_1_out[3]), .in_2(random_1_out[2]), .in_3(random_1_out[1]), .in_4(random_1_out[0]),
    .out_9(mostrador_1_out_9), .out_10(mostrador_1_out_10), .out_11(mostrador_1_out_11),
    .out_5(mostrador_1_out_5), .out_6(mostrador_1_out_6), .out_7(mostrador_1_out_7), .out_8(mostrador_1_out_8));
  L_19270569 l_19270569_1 (
    .in_1(in_1[2]), .in_2(random_1_out[2]), .out_3(l_19270569_1_out_3), .out_4(l_19270569_1_out_4));
  L_19270569 l_19270569_2 (
    .in_1(in_1[0]), .in_2(random_1_out[0]), .out_3(l_19270569_2_out_3), .out_4(l_19270569_2_out_4));
  L_00_ou_11_2cab960a l_00_ou_11_2cab960a_1 (
    .in_1(in_1[0]), .in_2(random_1_out[0]), .out_3(l_00_ou_11_2cab960a_1_out_3));
  L_00_ou_11_2cab960a l_00_ou_11_2cab960a_2 (
    .in_1(random_1_out[1]), .in_2(in_1[1]), .out_3(l_00_ou_11_2cab960a_2_out_3));
  L_00_ou_11_2cab960a l_00_ou_11_2cab960a_3 (
    .in_1(in_1[2]), .in_2(random_1_out[2]), .out_3(l_00_ou_11_2cab960a_3_out_3));
  L_00_ou_11_2cab960a l_00_ou_11_2cab960a_4 (
    .in_1(in_1[3]), .in_2(random_1_out[3]), .out_3(l_00_ou_11_2cab960a_4_out_3));
  L_19270569 l_19270569_3 (
    .in_1(in_1[3]), .in_2(random_1_out[3]), .out_3(l_19270569_3_out_3), .out_4(l_19270569_3_out_4));
  L_19270569 l_19270569_4 (
    .in_1(in_1[1]), .in_2(random_1_out[1]), .out_3(l_19270569_4_out_3), .out_4(l_19270569_4_out_4));
  and and_1 (out_2, l_00_ou_11_2cab960a_1_out_3, l_00_ou_11_2cab960a_2_out_3, l_00_ou_11_2cab960a_3_out_3, l_00_ou_11_2cab960a_4_out_3);
  L_6af18fe5 l_6af18fe5_1 (
    .in_2(l_19270569_3_out_3), .in_3(l_19270569_3_out_4), .in_1(out_2), .out_4(l_6af18fe5_1_out_4));
  L_6af18fe5 l_6af18fe5_2 (
    .in_2(l_19270569_1_out_3), .in_3(l_19270569_1_out_4), .in_1(l_6af18fe5_1_out_4),
    .out_4(l_6af18fe5_2_out_4));
  or mine (mine_out, l_6af18fe5_1_out_4, l_6af18fe5_2_out_4);
  or mine_2 (mine_2_out, mine_out, l_6af18fe5_3_out_4);
  L_6af18fe5 l_6af18fe5_3 (
    .in_2(l_19270569_4_out_3), .in_3(l_19270569_4_out_4), .in_1(mine_out), .out_4(l_6af18fe5_3_out_4));
  L_6af18fe5 l_6af18fe5_4 (
    .in_2(l_19270569_2_out_3), .in_3(l_19270569_2_out_4), .in_1(mine_2_out), .out_4(l_6af18fe5_4_out_4));
  and L_3e218025 (L_3e218025_out, l_19270569_3_out_3, l_6af18fe5_1_out_4);
  and L_bb417b61 (L_bb417b61_out, l_6af18fe5_1_out_4, l_19270569_3_out_4);
  and L_3e218025_2 (L_3e218025_2_out, l_19270569_1_out_3, l_6af18fe5_2_out_4);
  and L_bb417b61_2 (L_bb417b61_2_out, l_6af18fe5_2_out_4, l_19270569_1_out_4);
  and L_3e218025_3 (L_3e218025_3_out, l_19270569_4_out_3, l_6af18fe5_3_out_4);
  and L_bb417b61_3 (L_bb417b61_3_out, l_6af18fe5_3_out_4, l_19270569_4_out_4);
  and L_3e218025_4 (L_3e218025_4_out, l_19270569_2_out_3, l_6af18fe5_4_out_4);
  and L_bb417b61_4 (L_bb417b61_4_out, l_6af18fe5_4_out_4, l_19270569_2_out_4);
  or L_3e218025_5 (out_3, L_3e218025_out, L_3e218025_2_out, L_3e218025_3_out, L_3e218025_4_out);
  or L_bb417b61_5 (out_4, L_bb417b61_out, L_bb417b61_2_out, L_bb417b61_3_out, L_bb417b61_4_out);
endmodule

module L_19270569 (
  input  in_1,
  input  in_2,
  output out_3,
  output out_4
);

  wire not_1_out, not_2_out;

  not not_1 (not_1_out, in_2);
  not not_2 (not_2_out, in_1);
  and L_3e218025 (out_3, in_1, not_1_out);
  and L_bb417b61 (out_4, not_2_out, in_2);
endmodule

module L_00_ou_11_2cab960a (
  input  in_1,
  input  in_2,
  output out_3
);

  wire and_1_out, and_2_out, not_1_out, not_2_out;

  not not_1 (not_1_out, in_1);
  not not_2 (not_2_out, in_2);
  and and_1 (and_1_out, not_1_out, not_2_out);
  and and_2 (and_2_out, in_1, in_2);
  or or_1 (out_3, and_1_out, and_2_out);
endmodule

module Seg_Piso (
  input  A,
  input  B,
  input  C,
  input  D,
  output out_5
);

  wire and_1_out, and_2_out, and_3_out, and_4_out, and_5_out, and_6_out, not_1_out, not_2_out, not_3_out,
       not_4_out;

  not not_1 (not_1_out, A);
  not not_2 (not_2_out, B);
  not not_3 (not_3_out, C);
  not not_4 (not_4_out, D);
  and and_1 (and_1_out, A, B, not_3_out);
  and and_2 (and_2_out, not_1_out, not_2_out, C);
  and and_3 (and_3_out, B, not_3_out, D);
  and and_4 (and_4_out, not_2_out, not_3_out, not_4_out);
  and and_5 (and_5_out, B, C, not_4_out);
  and and_6 (and_6_out, A, not_2_out, D);
  or or_1 (out_5, and_1_out, and_2_out, and_3_out, and_4_out, and_5_out, and_6_out);
endmodule

module Seg_Teto (
  input  A,
  input  B,
  input  C,
  input  D,
  output out_5
);

  wire and_1_out, and_2_out, and_3_out, and_4_out, and_5_out, and_6_out, and_7_out, not_1_out, not_2_out,
       not_3_out, not_4_out;

  not not_1 (not_1_out, A);
  not not_2 (not_2_out, B);
  not not_3 (not_3_out, C);
  not not_4 (not_4_out, D);
  and and_1 (and_1_out, D, C, B);
  and and_2 (and_2_out, D, not_1_out, C);
  and and_3 (and_3_out, not_1_out, not_2_out, not_4_out);
  and and_4 (and_4_out, A, not_3_out, not_4_out);
  and and_5 (and_5_out, not_4_out, C);
  and and_6 (and_6_out, not_2_out, not_3_out, A);
  and and_7 (and_7_out, not_1_out, B, D);
  or or_1 (out_5, and_1_out, and_2_out, and_3_out, and_4_out, and_5_out, and_6_out, and_7_out);
endmodule

module Seg_Meio (
  input  A,
  input  B,
  input  C,
  input  D,
  output out_5
);

  wire and_1_out, and_2_out, and_3_out, and_4_out, and_5_out, not_1_out, not_2_out, not_3_out, not_4_out;

  not not_1 (not_1_out, A);
  not not_2 (not_2_out, B);
  not not_3 (not_3_out, C);
  not not_4 (not_4_out, D);
  and and_1 (and_1_out, A, not_2_out);
  and and_2 (and_2_out, not_3_out, B, not_1_out);
  and and_3 (and_3_out, not_1_out, not_2_out, C);
  and and_4 (and_4_out, C, not_4_out);
  and and_5 (and_5_out, A, B, D);
  or or_1 (out_5, and_1_out, and_2_out, and_3_out, and_4_out, and_5_out);
endmodule

module Seg_Dir_Baixo (
  input  A,
  input  B,
  input  C,
  input  D,
  output out_5
);

  wire and_1_out, and_2_out, and_3_out, and_4_out, and_5_out, not_1_out, not_2_out, not_3_out;

  not not_1 (not_1_out, A);
  not not_2 (not_2_out, B);
  not not_3 (not_3_out, C);
  and and_1 (and_1_out, not_1_out, B);
  and and_2 (and_2_out, not_1_out, not_2_out, not_3_out);
  and and_3 (and_3_out, not_2_out, A);
  and and_4 (and_4_out, not_3_out, D);
  and and_5 (and_5_out, not_1_out, C, D);
  or or_1 (out_5, and_1_out, and_2_out, and_3_out, and_4_out, and_5_out);
endmodule

module Seg_Esq_Baixo (
  input  A,
  input  B,
  input  C,
  input  D,
  output out_5
);

  wire and_1_out, and_2_out, and_3_out, and_4_out, not_2_out, not_3_out, not_4_out;

  // NOT_Gate not_1 has open pins: in=A, out=open
  not not_2 (not_2_out, B);
  not not_3 (not_3_out, C);
  not not_4 (not_4_out, D);
  and and_1 (and_1_out, A, not_2_out, C);
  and and_2 (and_2_out, A, B);
  and and_3 (and_3_out, not_2_out, not_3_out, not_4_out);
  and and_4 (and_4_out, C, not_4_out);
  or or_1 (out_5, and_1_out, and_2_out, and_3_out, and_4_out);
endmodule

module Seg_Dir_Cima (
  input  A,
  input  B,
  input  C,
  input  D,
  output out_5
);

  wire and_1_out, and_2_out, and_3_out, and_4_out, and_5_out, not_1_out, not_2_out, not_3_out, not_4_out;

  not not_1 (not_1_out, A);
  not not_2 (not_2_out, B);
  not not_3 (not_3_out, C);
  not not_4 (not_4_out, D);
  and and_1 (and_1_out, D, A, not_3_out);
  and and_2 (and_2_out, not_1_out, not_2_out);
  and and_3 (and_3_out, not_2_out, A, not_4_out);
  and and_4 (and_4_out, not_4_out, not_3_out, not_1_out);
  and and_5 (and_5_out, not_1_out, C, D);
  or or_1 (out_5, and_1_out, and_2_out, and_3_out, and_4_out, and_5_out);
endmodule

module Seg_Esq_Cima (
  input  A,
  input  B,
  input  C,
  input  D,
  output out_5
);

  wire and_1_out, and_2_out, and_3_out, and_4_out, and_5_out, not_1_out, not_2_out, not_3_out, not_4_out;

  not not_1 (not_1_out, A);
  not not_2 (not_2_out, B);
  not not_3 (not_3_out, C);
  not not_4 (not_4_out, D);
  and and_1 (and_1_out, A, not_2_out);
  and and_2 (and_2_out, not_1_out, B, not_3_out);
  and and_3 (and_3_out, B, not_4_out, C);
  and and_4 (and_4_out, not_3_out, not_4_out);
  and and_5 (and_5_out, A, B, C);
  or or_1 (out_5, and_1_out, and_2_out, and_3_out, and_4_out, and_5_out);
endmodule

module Mostrador (
  input  in_1,
  input  in_2,
  input  in_3,
  input  in_4,
  output out_5,
  output out_6,
  output out_7,
  output out_8,
  output out_9,
  output out_10,
  output out_11
);

  Seg_Meio seg_meio_1 (.A(in_1), .B(in_2), .C(in_3), .D(in_4), .out_5(out_5));
  Seg_Esq_Cima seg_esq_cima_1 (.A(in_1), .B(in_2), .C(in_3), .D(in_4), .out_5(out_6));
  Seg_Dir_Cima seg_dir_cima_1 (.A(in_1), .B(in_2), .C(in_3), .D(in_4), .out_5(out_8));
  Seg_Teto seg_teto_1 (.A(in_1), .B(in_2), .C(in_3), .D(in_4), .out_5(out_7));
  Seg_Dir_Baixo seg_dir_baixo_1 (.A(in_1), .B(in_2), .C(in_3), .D(in_4), .out_5(out_11));
  Seg_Piso seg_piso_1 (.A(in_1), .B(in_2), .C(in_3), .D(in_4), .out_5(out_10));
  Seg_Esq_Baixo seg_esq_baixo_1 (.A(in_1), .B(in_2), .C(in_3), .D(in_4), .out_5(out_9));
endmodule

module relojo6 (
  input  clk,
  input  f_18,
  input  in_3,
  input  [3:0] usu,
  input  \config ,
  output [3:0] out_6,
  output _0,
  output _6
);

  wire and_1_out, and_2_out, and_3_out, or_1_out;
  wire [3:0] com_bot_o_7b0cf85d_1_out_4, com_bot_o_7b0cf85d_2_out_4, subtractor_1_out, subtractor_2_out;

  com_bot_o_7b0cf85d com_bot_o_7b0cf85d_1 (
    .in_2(com_bot_o_7b0cf85d_2_out_4), .in_3(usu), .in_1(\config ), .out_4(com_bot_o_7b0cf85d_1_out_4));
  and and_1 (and_1_out, clk, ~and_2_out);  // AND_Gate
  and and_2 (and_2_out, f_18, in_3, _0);
  and and_3 (and_3_out, clk, \config );
  or or_1 (or_1_out, and_3_out, and_1_out);
  D_Flip_Flop d_ff_1 (.clk(or_1_out), .D(com_bot_o_7b0cf85d_1_out_4[0]), .Q(out_6[0]));  // open: Qn, preset, en, reset
  D_Flip_Flop d_ff_2 (.clk(or_1_out), .D(com_bot_o_7b0cf85d_1_out_4[1]), .Q(out_6[1]));  // open: Qn, preset, en, reset
  D_Flip_Flop d_ff_3 (.clk(or_1_out), .D(com_bot_o_7b0cf85d_1_out_4[2]), .Q(out_6[2]));  // open: Qn, preset, en, reset
  and and_4 (_6, out_6[2], ~out_6[1], out_6[0], ~com_bot_o_7b0cf85d_1_out_4[3]);  // AND_Gate
  D_Flip_Flop d_ff_4 (.clk(or_1_out), .D(com_bot_o_7b0cf85d_1_out_4[3]), .Q(out_6[3]));  // open: Qn, preset, en, reset
  and and_5 (_0, ~out_6[0], ~out_6[1], ~out_6[2]);  // AND_Gate
  com_bot_o_7b0cf85d com_bot_o_7b0cf85d_2 (
    .in_2(subtractor_2_out), .in_3(subtractor_1_out), .in_1(_0), .out_4(com_bot_o_7b0cf85d_2_out_4));
  Subtractor #(.width(4)) subtractor_1 (.a(out_6), .b(4'b1011), .out(subtractor_1_out));  // open: bin, bout
  Hex_Digit_Display hex_digit_display_1 (.value(out_6));  // open: dp
  Subtractor #(.width(4)) subtractor_2 (.a(out_6), .b(4'b0001), .out(subtractor_2_out));  // open: bin, bout
endmodule

module relogio_9 (
  input  clk,
  input  de_f,
  input  in_3,
  input  in_4,
  input  [3:0] usu,
  input  \config ,
  output [3:0] sai,
  output _0,
  output _9
);

  wire and_1_out, and_2_out, and_3_out, or_1_out;
  wire [3:0] com_bot_o_7b0cf85d_1_out_4, com_bot_o_7b0cf85d_2_out_4, subtractor_1_out, subtractor_2_out;

  and and_1 (and_1_out, clk, ~and_2_out);  // AND_Gate
  and and_2 (and_2_out, in_3, de_f, _0, in_4);
  com_bot_o_7b0cf85d com_bot_o_7b0cf85d_1 (
    .in_2(com_bot_o_7b0cf85d_2_out_4), .in_3(usu), .in_1(\config ), .out_4(com_bot_o_7b0cf85d_1_out_4));
  and and_3 (and_3_out, clk, \config );
  or or_1 (or_1_out, and_3_out, and_1_out);
  D_Flip_Flop d_ff_1 (.clk(or_1_out), .D(com_bot_o_7b0cf85d_1_out_4[0]), .Q(sai[0]));  // open: Qn, preset, en, reset
  D_Flip_Flop d_ff_2 (.clk(or_1_out), .D(com_bot_o_7b0cf85d_1_out_4[1]), .Q(sai[1]));  // open: Qn, preset, en, reset
  D_Flip_Flop d_ff_3 (.clk(or_1_out), .D(com_bot_o_7b0cf85d_1_out_4[2]), .Q(sai[2]));  // open: Qn, preset, en, reset
  and and_4 (_9, ~sai[1], sai[0], ~sai[2], sai[3]);  // AND_Gate
  D_Flip_Flop d_ff_4 (.clk(or_1_out), .D(com_bot_o_7b0cf85d_1_out_4[3]), .Q(sai[3]));  // open: Qn, preset, en, reset
  and and_5 (_0, ~sai[0], ~sai[2], ~sai[3], ~sai[1]);  // AND_Gate
  com_bot_o_7b0cf85d com_bot_o_7b0cf85d_2 (
    .in_2(subtractor_2_out), .in_3(subtractor_1_out), .in_1(_0), .out_4(com_bot_o_7b0cf85d_2_out_4));
  Subtractor #(.width(4)) subtractor_1 (.a(sai), .b(4'b0111), .out(subtractor_1_out));  // open: bin, bout
  Hex_Digit_Display hex_digit_display_1 (.value(sai));  // open: dp
  Subtractor #(.width(4)) subtractor_2 (.a(sai), .b(4'b0001), .out(subtractor_2_out));  // open: bin, bout
endmodule

module cot_9 (
  input  clk,
  output [3:0] out_2,
  output out_3
);

  wire and_1_out;
  wire [3:0] adder_1_out, adder_2_out, com_bot_o_7b0cf85d_1_out_4;

  D_Flip_Flop d_ff_1 (.clk(clk), .D(com_bot_o_7b0cf85d_1_out_4[0]), .Q(out_2[0]));  // open: Qn, preset, en, reset
  D_Flip_Flop d_ff_2 (.clk(clk), .D(com_bot_o_7b0cf85d_1_out_4[1]), .Q(out_2[1]));  // open: Qn, preset, en, reset
  D_Flip_Flop d_ff_3 (.clk(clk), .D(com_bot_o_7b0cf85d_1_out_4[2]), .Q(out_2[2]));  // open: Qn, preset, en, reset
  D_Flip_Flop d_ff_4 (.clk(clk), .D(com_bot_o_7b0cf85d_1_out_4[3]), .Q(out_2[3]));  // open: Qn, preset, en, reset
  and and_1 (and_1_out, out_2[0], ~out_2[2], out_2[3], ~out_2[1]);  // AND_Gate
  com_bot_o_7b0cf85d com_bot_o_7b0cf85d_1 (
    .in_2(adder_2_out), .in_3(adder_1_out), .in_1(and_1_out), .out_4(com_bot_o_7b0cf85d_1_out_4));
  Adder #(.width(4)) adder_1 (.a(out_2), .b(4'b0111), .out(adder_1_out));  // open: cin, cout
  and and_2 (out_3, ~out_2[0], ~out_2[3], ~out_2[2], ~out_2[1]);  // AND_Gate
  Hex_Digit_Display hex_digit_display_1 (.value(out_2));  // open: dp
  Adder #(.width(4)) adder_2 (.a(out_2), .b(4'b0001), .out(adder_2_out));  // open: cin, cout
endmodule

module cot_6 (
  input  clk,
  output [3:0] out_2,
  output out_3
);

  wire and_1_out;
  wire [3:0] adder_1_out, adder_2_out, com_bot_o_7b0cf85d_1_out_4;

  D_Flip_Flop d_ff_1 (.clk(clk), .D(com_bot_o_7b0cf85d_1_out_4[0]), .Q(out_2[0]));  // open: Qn, preset, en, reset
  D_Flip_Flop d_ff_2 (.clk(clk), .D(com_bot_o_7b0cf85d_1_out_4[1]), .Q(out_2[1]));  // open: Qn, preset, en, reset
  D_Flip_Flop d_ff_3 (.clk(clk), .D(com_bot_o_7b0cf85d_1_out_4[2]), .Q(out_2[2]));  // open: Qn, preset, en, reset
  D_Flip_Flop d_ff_4 (.clk(clk), .D(com_bot_o_7b0cf85d_1_out_4[3]), .Q(out_2[3]));  // open: Qn, preset, en, reset
  and and_1 (and_1_out, out_2[0], ~out_2[1], out_2[2]);  // AND_Gate
  com_bot_o_7b0cf85d com_bot_o_7b0cf85d_1 (
    .in_2(adder_2_out), .in_3(adder_1_out), .in_1(and_1_out), .out_4(com_bot_o_7b0cf85d_1_out_4));
  Adder #(.width(4)) adder_1 (.a(out_2), .b(4'b1011), .out(adder_1_out));  // open: cin, cout
  and and_2 (out_3, ~out_2[0], ~out_2[1], ~out_2[2]);  // AND_Gate
  Hex_Digit_Display hex_digit_display_1 (.value(out_2));  // open: dp
  Adder #(.width(4)) adder_2 (.a(out_2), .b(4'b0001), .out(adder_2_out));  // open: cin, cout
endmodule

module alavan (
  input  in_1,
  output out_2
);

  wire d_ff_1_q;

  D_Flip_Flop d_ff_1 (.clk(in_1), .D(out_2), .Q(d_ff_1_q));  // open: Qn, preset, en, reset
  not not_1 (out_2, d_ff_1_q);
endmodule

module rlogio_9_esp (
  input  clk,
  input  [3:0] usu,
  input  \config ,
  output [3:0] sai,
  output out_5,
  output out_6
);

  wire and_1_out, and_2_out, or_1_out;
  wire [3:0] com_bot_o_7b0cf85d_1_out_4, com_bot_o_7b0cf85d_2_out_4, subtractor_1_out, subtractor_2_out;

  com_bot_o_7b0cf85d com_bot_o_7b0cf85d_1 (
    .in_2(com_bot_o_7b0cf85d_2_out_4), .in_3(usu), .in_1(\config ), .out_4(com_bot_o_7b0cf85d_1_out_4));
  and and_1 (and_1_out, clk, ~out_6);  // AND_Gate
  and and_2 (and_2_out, clk, \config );
  or or_1 (or_1_out, and_1_out, and_2_out);
  D_Flip_Flop d_ff_1 (.clk(or_1_out), .D(com_bot_o_7b0cf85d_1_out_4[0]), .Q(sai[0]));  // open: Qn, preset, en, reset
  D_Flip_Flop d_ff_2 (.clk(or_1_out), .D(com_bot_o_7b0cf85d_1_out_4[1]), .Q(sai[1]));  // open: Qn, preset, en, reset
  D_Flip_Flop d_ff_3 (.clk(or_1_out), .D(com_bot_o_7b0cf85d_1_out_4[2]), .Q(sai[2]));  // open: Qn, preset, en, reset
  and and_3 (out_6, ~sai[1], ~sai[0], ~sai[2], ~sai[3]);  // AND_Gate
  D_Flip_Flop d_ff_4 (.clk(or_1_out), .D(com_bot_o_7b0cf85d_1_out_4[3]), .Q(sai[3]));  // open: Qn, preset, en, reset
  and and_4 (out_5, ~sai[0], ~sai[2], ~sai[3], ~sai[1]);  // AND_Gate
  com_bot_o_7b0cf85d com_bot_o_7b0cf85d_2 (
    .in_2(subtractor_2_out), .in_3(subtractor_1_out), .in_1(out_5), .out_4(com_bot_o_7b0cf85d_2_out_4));
  Subtractor #(.width(4)) subtractor_1 (.a(sai), .b(4'b0111), .out(subtractor_1_out));  // open: bin, bout
  Hex_Digit_Display hex_digit_display_1 (.value(sai));  // open: dp
  Subtractor #(.width(4)) subtractor_2 (.a(sai), .b(4'b0001), .out(subtractor_2_out));  // open: bin, bout
endmodule

module JJJJJ (
  input  in_1,
  input  in_2,
  input  in_3,
  output [2:0] out_4
);

  wire [2:0] not_1_out;

  not not_1 (not_1_out[0], in_1);
  not not_2 (not_1_out[1], in_2);
  not not_3 (not_1_out[2], in_3);
  Adder #(.width(3)) adder_1 (.a(3'b001), .b(not_1_out), .out(out_4));  // open: cin, cout
endmodule

module TTTTT (
  input  [3:0] in_1,
  input  [3:0] in_2,
  input  [3:0] in_3,
  input  [3:0] in_4,
  output out_5
);

  wire or_1_out, or_2_out, or_3_out, or_4_out, or_5_out;

  or or_1 (or_1_out, in_1[3], in_1[2], in_1[1], in_1[0]);
  or or_2 (or_2_out, in_2[3], in_2[2], in_2[1], in_2[0]);
  or or_3 (or_3_out, or_1_out, or_2_out, or_4_out, or_5_out);
  or or_4 (or_4_out, in_3[3], in_3[2], in_3[1], in_3[0]);
  or or_5 (or_5_out, in_4[3], in_4[2], in_4[1], in_4[0]);
  not not_1 (out_5, or_3_out);
endmodule

module TESTE_1 (
  input  [3:0] in_1,
  output [3:0] out_2
);

  wire [2:0] jjjjj_1_out_4;

  JJJJJ jjjjj_1 (.in_1(in_1[0]), .in_2(in_1[1]), .in_3(in_1[2]), .out_4(jjjjj_1_out_4));
  com_bot_o_7b0cf85d com_bot_o_7b0cf85d_1 (.in_2(in_1), .in_3({1'b0, jjjjj_1_out_4}), .in_1(in_1[3]), .out_4(out_2));
endmodule

module Demultiplexador (
  input  [3:0] in_1,
  input  in_2,
  output [3:0] out_3,
  output [3:0] out_4
);

  SLSLS slsls_1 (.in_1(in_1[0]), .in_2(in_2), .out_3(out_4[0]), .out_4(out_3[0]));
  SLSLS slsls_2 (.in_1(in_1[1]), .in_2(in_2), .out_3(out_4[1]), .out_4(out_3[1]));
  SLSLS slsls_3 (.in_1(in_1[2]), .in_2(in_2), .out_3(out_4[2]), .out_4(out_3[2]));
  SLSLS slsls_4 (.in_1(in_1[3]), .in_2(in_2), .out_3(out_4[3]), .out_4(out_3[3]));
endmodule

module SLSLS (
  input  in_1,
  input  in_2,
  output out_3,
  output out_4
);

  and and_1 (out_3, in_1, ~in_2);  // AND_Gate
  and and_2 (out_4, in_2, in_1);
endmodule

module KKKKK (
  input  in_1,
  input  in_2,
  input  in_3,
  input  in_4,
  input  in_5,
  output out_6,
  output out_7,
  output [3:0] out_8,
  output [3:0] out_9
);

  wire alavan_1_out_2, not_1_out, not_2_out, slsls_1_out_3, slsls_1_out_4;
  wire [3:0] teste_1_1_out_2;

  LED led_1 (.in(in_2));
  Hex_Digit_Display hex_digit_display_1 (.value(out_8));  // open: dp
  YAYA yaya_1 (.in_2(alavan_1_out_2), .in_1(teste_1_1_out_2), .out_3(out_8));
  D_Flip_Flop d_ff_1 (.clk(alavan_1_out_2), .D(slsls_1_out_3), .Q(out_6));  // open: Qn, preset, en, reset
  not not_1 (not_1_out, alavan_1_out_2);
  SLSLS slsls_1 (.in_1(in_2), .in_2(alavan_1_out_2), .out_3(slsls_1_out_3), .out_4(slsls_1_out_4));
  TESTE_1 teste_1_1 (.out_2(teste_1_1_out_2), .in_1({in_2, in_3, in_4, in_5}));
  YAYA yaya_2 (.in_2(not_2_out), .in_1(teste_1_1_out_2), .out_3(out_9));
  not not_2 (not_2_out, alavan_1_out_2);
  D_Flip_Flop d_ff_2 (.clk(not_1_out), .D(slsls_1_out_4), .Q(out_7));  // open: Qn, preset, en, reset
  alavan alavan_1 (.in_1(in_1), .out_2(alavan_1_out_2));
  Hex_Digit_Display hex_digit_display_2 (.value(out_9));  // open: dp
endmodule

module YAYA (
  input  [3:0] in_1,
  input  in_2,
  output [3:0] out_3
);

  D_Flip_Flop d_ff_1 (.clk(in_2), .D(in_1[3]), .Q(out_3[3]));  // open: Qn, preset, en, reset
  D_Flip_Flop d_ff_2 (.clk(in_2), .D(in_1[2]), .Q(out_3[2]));  // open: Qn, preset, en, reset
  D_Flip_Flop d_ff_3 (.clk(in_2), .D(in_1[1]), .Q(out_3[1]));  // open: Qn, preset, en, reset
  D_Flip_Flop d_ff_4 (.clk(in_2), .D(in_1[0]), .Q(out_3[0]));  // open: Qn, preset, en, reset
endmodule

module MAOISOI (
  input  [3:0] in_1,
  input  [3:0] in_2
);

  wire alavan_1_out_2, button_1_out, iguais_1_out_3, iguais_2_out_3, iguais_3_out_3, kkkkk_1_out_6,
       kkkkk_1_out_7, not_1_out, not_2_out, or_1_out;
  wire [3:0] adder_1_out, com_bot_o_7b0cf85d_1_out_4, com_bot_o_7b0cf85d_2_out_4, d_ff_1_q, kkkkk_1_out_8,
       kkkkk_1_out_9;

  LED A_jogando (.in(or_1_out));
  LED B_jogando (.in(not_1_out));
  D_Flip_Flop d_ff_1 (
    .clk(button_1_out), .D(com_bot_o_7b0cf85d_2_out_4[0]), .Q(d_ff_1_q[0]));  // open: Qn, preset, en, reset
  not not_1 (not_1_out, or_1_out);
  LED \Posição_X  (.in(alavan_1_out_2));
  LED led_1 (.in(kkkkk_1_out_7));
  Hex_Digit_Display hex_digit_display_1 (.value(kkkkk_1_out_9));  // open: dp
  com_bot_o_7b0cf85d com_bot_o_7b0cf85d_1 (
    .in_2(in_2), .in_3(in_1), .in_1(or_1_out), .out_4(com_bot_o_7b0cf85d_1_out_4));
  D_Flip_Flop d_ff_2 (
    .clk(button_1_out), .D(com_bot_o_7b0cf85d_2_out_4[1]), .Q(d_ff_1_q[1]));  // open: Qn, preset, en, reset
  not not_2 (not_2_out, alavan_1_out_2);
  LED \Posição_Y  (.in(not_2_out));
  LED led_2 (.in(kkkkk_1_out_6));
  Hex_Digit_Display hex_digit_display_2 (.value(kkkkk_1_out_8));  // open: dp
  KKKKK kkkkk_1 (
    .out_6(kkkkk_1_out_6), .out_8(kkkkk_1_out_8), .out_9(kkkkk_1_out_9),
    .in_2(com_bot_o_7b0cf85d_1_out_4[3]), .in_3(com_bot_o_7b0cf85d_1_out_4[2]),
    .in_4(com_bot_o_7b0cf85d_1_out_4[1]), .in_5(com_bot_o_7b0cf85d_1_out_4[0]), .out_7(kkkkk_1_out_7),
    .in_1(button_1_out));
  D_Flip_Flop d_ff_3 (
    .clk(button_1_out), .D(com_bot_o_7b0cf85d_2_out_4[2]), .Q(d_ff_1_q[2]));  // open: Qn, preset, en, reset
  alavan alavan_1 (.in_1(button_1_out), .out_2(alavan_1_out_2));
  iguais iguais_1 (.in_1(d_ff_1_q), .in_2(4'b0000), .out_3(iguais_1_out_3));
  Button button_1 (.out(button_1_out));
  D_Flip_Flop d_ff_4 (
    .clk(button_1_out), .D(com_bot_o_7b0cf85d_2_out_4[3]), .Q(d_ff_1_q[3]));  // open: Qn, preset, en, reset
  or or_1 (or_1_out, iguais_1_out_3, iguais_2_out_3);
  iguais iguais_2 (.in_1(d_ff_1_q), .in_2(4'b0001), .out_3(iguais_2_out_3));
  Adder #(.width(4)) adder_1 (.a(d_ff_1_q), .b(4'b0001), .out(adder_1_out));  // open: cin, cout
  iguais iguais_3 (.in_1(adder_1_out), .in_2(4'b0100), .out_3(iguais_3_out_3));
  com_bot_o_7b0cf85d com_bot_o_7b0cf85d_2 (
    .in_2(adder_1_out), .in_3(4'b0000), .in_1(iguais_3_out_3), .out_4(com_bot_o_7b0cf85d_2_out_4));
endmodule

module iguais (
  input  [3:0] in_1,
  input  [3:0] in_2,
  output out_3
);

  wire xnor_1_out, xnor_2_out, xnor_3_out, xnor_4_out;

  xnor xnor_1 (xnor_1_out, in_1[0], in_2[0]);
  xnor xnor_2 (xnor_2_out, in_1[1], in_2[1]);
  xnor xnor_3 (xnor_3_out, in_1[2], in_2[2]);
  xnor xnor_4 (xnor_4_out, in_2[3], in_1[3]);
  and and_1 (out_3, xnor_1_out, xnor_2_out, xnor_3_out, xnor_4_out);
endmodule
