// Logisim project trabalho2.8.circ as structural Verilog: 40 circuits, main circuit main
module com_bot_o_7b0cf85d (
  input  in_1,
  input  [3:0] in_2,
  input  [3:0] in_3,
  output [3:0] out_4
);

  wire not_1_out, not_2_out, not_3_out, not_4_out;

  not not_1 (not_1_out, in_1);
  not not_2 (not_2_out, not_1_out);
  not not_3 (not_3_out, not_2_out);
  not not_4 (not_4_out, not_3_out);
  triangulo triangulo_1 (.in_2(in_2[0]), .in_3(in_3[0]), .in_1(not_4_out), .out_4(out_4[0]));
  triangulo triangulo_2 (.in_2(in_2[1]), .in_3(in_3[1]), .in_1(not_4_out), .out_4(out_4[1]));
  triangulo triangulo_3 (.in_2(in_2[2]), .in_3(in_3[2]), .in_1(not_4_out), .out_4(out_4[2]));
  triangulo triangulo_4 (.in_2(in_2[3]), .in_3(in_3[3]), .in_1(not_4_out), .out_4(out_4[3]));
endmodule

module main (
  input  in_1,
  output [3:0] out_2,
  output [3:0] out_3,
  output [3:0] out_4,
  output [3:0] out_5,
  output out_6
);

  wire alavan_1_out_2, and_1_out, and_2_out, button_1_out, button_2_out, button_3_out, button_4_out,
       button_5_out, c6_out_3, c9_2_out_3, c9_3_out_3, clock_1_out, or_1_out, or_2_out, or_3_out, or_4_out,
       relogio_9_1__0, relogio_9_1__9, relogio_9_2__9, relojo6_1__0, relojo6_1__6, rlogio_9_esp_1_out_5,
       rlogio_9_esp_1_out_6, xor_1_out, xor_2_out, xor_3_out;
  wire [3:0] c6_out_2, c9_2_out_2, c9_3_out_2, c9_out_2;

  xor xor_1 (xor_1_out, button_1_out, c9_2_out_3);
  cot_9 c9 (.clk(xor_1_out), .out_2(c9_out_2));  // open: out_3
  Hex_Digit_Display hex_digit_display_1 (.value(c9_out_2));  // open: dp
  or or_1 (or_1_out, relogio_9_1__9, and_1_out);
  rlogio_9_esp rlogio_9_esp_1 (
    .clk(or_1_out), .out_5(rlogio_9_esp_1_out_5), .\config (alavan_1_out_2), .out_6(rlogio_9_esp_1_out_6),
    .sai(out_2), .usu(c9_out_2));
  Hex_Digit_Display hex_digit_display_2 (.value(out_2));  // open: dp
  cot_9 c9_2 (.clk(xor_2_out), .out_2(c9_2_out_2), .out_3(c9_2_out_3));
  Button button_1 (.out(button_1_out));
  Hex_Digit_Display hex_digit_display_3 (.value(c9_2_out_2));  // open: dp
  or or_2 (or_2_out, and_1_out, relojo6_1__6);
  Hex_Digit_Display hex_digit_display_4 (.value(out_3));  // open: dp
  xor xor_2 (xor_2_out, button_2_out, c6_out_3);
  cot_6 c6 (.clk(xor_3_out), .out_2(c6_out_2), .out_3(c6_out_3));
  Button button_2 (.out(button_2_out));
  Hex_Digit_Display hex_digit_display_5 (.value(c6_out_2));  // open: dp
  or or_3 (or_3_out, relogio_9_2__9, and_1_out);
  relogio_9 relogio_9_1 (
    .clk(or_2_out), .in_3(rlogio_9_esp_1_out_6), .in_4(rlogio_9_esp_1_out_5), .sai(out_3),
    ._0(relogio_9_1__0), .usu(c9_2_out_2), .\config (alavan_1_out_2), ._9(relogio_9_1__9));  // open: de_f
  Hex_Digit_Display hex_digit_display_6 (.value(out_4));  // open: dp
  xor xor_3 (xor_3_out, button_3_out, c9_3_out_3);
  Button button_3 (.out(button_3_out));
  Hex_Digit_Display hex_digit_display_7 (.value(c9_3_out_2));  // open: dp
  or or_4 (or_4_out, and_2_out, and_1_out);
  relojo6 relojo6_1 (
    .clk(or_3_out), .f_18(relogio_9_1__0), .in_3(rlogio_9_esp_1_out_6), .\config (alavan_1_out_2),
    ._6(relojo6_1__6), .out_6(out_4), .usu(c6_out_2), ._0(relojo6_1__0));
  TTTTT ttttt_1 (.in_1(out_2), .in_2(out_3), .in_3(out_4), .in_4(out_5), .out_5(out_6));
  cot_9 c9_3 (.clk(button_4_out), .out_2(c9_3_out_2), .out_3(c9_3_out_3));
  Button button_4 (.out(button_4_out));
  relogio_9 relogio_9_2 (
    .clk(or_4_out), .de_f(relojo6_1__0), .in_3(relogio_9_1__0), .in_4(rlogio_9_esp_1_out_6), .sai(out_5),
    .usu(c9_3_out_2), .\config (alavan_1_out_2), ._9(relogio_9_2__9));  // open: _0
  and and_1 (and_1_out, clock_1_out, alavan_1_out_2);
  Hex_Digit_Display hex_digit_display_8 (.value(out_5));  // open: dp
  and and_2 (and_2_out, in_1, clock_1_out);
  alavan alavan_1 (.in_1(button_5_out), .out_2(alavan_1_out_2));
  Button button_5 (.out(button_5_out));
  Clock clock_1 (.out(clock_1_out));
endmodule

module triangulo (
  input  in_1,
  input  in_2,
  input  in_3,
  output out_4
);

  wire and_1_out, and_2_out, and_3_out, and_4_out, not_1_out, not_2_out, not_3_out, not_4_out;

  not not_1 (not_1_out, in_1);
  and and_1 (and_1_out, in_1, in_3, not_2_out);
  not not_2 (not_2_out, in_2);
  and and_2 (and_2_out, not_1_out, in_2, not_3_out);
  not not_3 (not_3_out, in_3);
  not not_4 (not_4_out, in_1);
  and and_3 (and_3_out, not_4_out, in_2, in_3);
  and and_4 (and_4_out, in_1, in_2, in_3);
  or or_1 (out_4, and_1_out, and_2_out, and_3_out, and_4_out);
endmodule

module L_6af18fe5 (
  input  in_1,
  input  in_2,
  input  in_3,
  output out_4
);

  wire and_1_out, and_2_out, not_1_out, not_2_out, not_3_out, not_4_out, or_1_out;

  not not_1 (not_1_out, in_2);
  not not_2 (not_2_out, in_3);
  and and_1 (and_1_out, not_1_out, not_2_out);
  and and_2 (and_2_out, in_2, in_3);
  or or_1 (or_1_out, and_2_out, and_1_out, and_1_out, and_1_out);
  not not_3 (not_3_out, or_1_out);
  not not_4 (not_4_out, in_1);
  and and_3 (out_4, not_3_out, not_4_out);
endmodule

module L_d_7ebe929a (
  input  [3:0] in_1,
  output out_2,
  output out_3,
  output out_4
);

  wire l_00_ou_11_2cab960a_1_out_3, l_00_ou_11_2cab960a_2_out_3, l_00_ou_11_2cab960a_3_out_3,
       l_00_ou_11_2cab960a_4_out_3, L_3e218025_2_out, L_3e218025_3_out, L_3e218025_4_out, L_3e218025_out,
       l_6af18fe5_1_out_4, l_6af18fe5_2_out_4, l_6af18fe5_3_out_4, l_6af18fe5_4_out_4, l_19270569_1_out_3,
       l_19270569_1_out_4, l_19270569_2_out_3, l_19270569_2_out_4, l_19270569_3_out_3, l_19270569_3_out_4,
       l_19270569_4_out_3, l_19270569_4_out_4, L_bb417b61_2_out, L_bb417b61_3_out, L_bb417b61_4_out,
       L_bb417b61_out, mine_2_out, mine_out, mostrador_1_out_5, mostrador_1_out_6, mostrador_1_out_7,
       mostrador_1_out_8, mostrador_1_out_9, mostrador_1_out_10, mostrador_1_out_11;
  wire [3:0] random_1_out;

  Random #(.width(4), .seed(42)) random_1 (.out(random_1_out));  // open: clk, next, clr
  _7_Segment_Display u_7_segment_display_1 (
    .g(mostrador_1_out_8), .f(mostrador_1_out_7), .a(mostrador_1_out_6), .b(mostrador_1_out_5),
    .e(mostrador_1_out_11), .d(mostrador_1_out_10), .c(mostrador_1_out_9));  // open: dp
  Mostrador mostrador_1 (
    .in_1(random_1_out[3]), .in_2(random_1_out[2]), .in_3(random_1_out[1]), .in_4(random_1_out[0]),
    .out_9(mostrador_1_out_9), .out_10(mostrador_1_out_10), .out_11(mostrador_1_out_11),
    .out_5(mostrador_1_out_5), .out_6(mostrador_1_out_6), .out_7(mostrador_1_out_7), .out_8(mostrador_1_out_8));
  L_19270569 l_19270569_1 (
    .in_1(in_1[2]), .in_2(random_1_out[2]), .out_3(l_19270569_1_out_3), .out_4(l_19270569_1_out_4));
  L_19270569 l_19270569_2 (
    .in_1(in_1[0]), .in_2(random_1_out[0]), .out_3(l_19270569_2_out_3), .out_4(l_19270569_2_out_4));
  L_00_ou_11_2cab960a l_00_ou_11_2cab960a_1 (
    .in_1(in_1[0]), .in_2(random_1_out[0]), .out_3(l_00_ou_11_2cab960a_1_out_3));
  L_00_ou_11_2cab960a l_00_ou_11_2cab960a_2 (
    .in_1(random_1_out[1]), .in_2(in_1[1]), .out_3(l_00_ou_11_2cab960a_2_out_3));
  L_00_ou_11_2cab960a l_00_ou_11_2cab960a_3 (
    .in_1(in_1[2]), .in_2(random_1_out[2]), .out_3(l_00_ou_11_2cab960a_3_out_3));
  L_00_ou_11_2cab960a l_00_ou_11_2cab960a_4 (
    .in_1(in_1[3]), .in_2(random_1_out[3]), .out_3(l_00_ou_11_2cab960a_4_out_3));
  L_19270569 l_19270569_3 (
    .in_1(in_1[3]), .in_2(random_1_out[3]), .out_3(l_19270569_3_out_3), .out_4(l_19270569_3_out_4));
  L_19270569 l_19270569_4 (
    .in_1(in_1[1]), .in_2(random_1_out[1]), .out_3(l_19270569_4_out_3), .out_4(l_19270569_4_out_4));
  and and_1 (out_2, l_00_ou_11_2cab960a_1_out_3, l_00_ou_11_2cab960a_2_out_3, l_00_ou_11_2cab960a_3_out_3, l_00_ou_11_2cab960a_4_out_3);
  L_6af18fe5 l_6af18fe5_1 (
    .in_2(l_19270569_3_out_3), .in_3(l_19270569_3_out_4), .in_1(out_2), .out_4(l_6af18fe5_1_out_4));
  L_6af18fe5 l_6af18fe5_2 (
    .in_2(l_19270569_1_out_3), .in_3(l_19270569_1_out_4), .in_1(l_6af18fe5_1_out_4),
    .out_4(l_6af18fe5_2_out_4));
  or mine (mine_out, l_6af18fe5_1_out_4, l_6af18fe5_2_out_4);
  or mine_2 (mine_2_out, mine_out, l_6af18fe5_3_out_4);
  L_6af18fe5 l_6af18fe5_3 (
    .in_2(l_19270569_4_out_3), .in_3(l_19270569_4_out_4), .in_1(mine_out), .out_4(l_6af18fe5_3_out_4));
  L_6af18fe5 l_6af18fe5_4 (
    .in_2(l_19270569_2_out_3), .in_3(l_19270569_2_out_4), .in_1(mine_2_out), .out_4(l_6af18fe5_4_out_4));
  and L_3e218025 (L_3e218025_out, l_19270569_3_out_3, l_6af18fe5_1_out_4);
  and L_bb417b61 (L_bb417b61_out, l_6af18fe5_1_out_4, l_19270569_3_out_4);
  and L_3e218025_2 (L_3e218025_2_out, l_19270569_1_out_3, l_6af18fe5_2_out_4);
  and L_bb417b61_2 (L_bb417b61_2_out, l_6af18fe5_2_out_4, l_19270569_1_out_4);
  and L_3e218025_3 (L_3e218025_3_out, l_19270569_4_out_3, l_6af18fe5_3_out_4);
  and L_bb417b61_3 (L_bb417b61_3_out, l_6af18fe5_3_out_4, l_19270569_4_out_4);
  and L_3e218025_4 (L_3e218025_4_out, l_19270569_2_out_3, l_6af18fe5_4_out_4);
  and L_bb417b61_4 (L_bb417b61_4_out, l_6af18fe5_4_out_4, l_19270569_2_out_4);
  or L_3e218025_5 (out_3, L_3e218025_out, L_3e218025_2_out, L_3e218025_3_out, L_3e218025_4_out);
  or L_bb417b61_5 (out_4, L_bb417b61_out, L_bb417b61_2_out, L_bb417b61_3_out, L_bb417b61_4_out);
endmodule

module L_19270569 (
  input  in_1,
  input  in_2,
  output out_3,
  output out_4
);

  wire not_1_out, not_2_out;

  not not_1 (not_1_out, in_2);
  not not_2 (not_2_out, in_1);
  and L_3e218025 (out_3, in_1, not_1_out);
  and L_bb417b61 (out_4, not_2_out, in_2);
endmodule

module L_00_ou_11_2cab960a (
  input  in_1,
  input  in_2,
  output out_3
);

  wire and_1_out, and_2_out, not_1_out, not_2_out;

  not not_1 (not_1_out, in_1);
  not not_2 (not_2_out, in_2);
  and and_1 (and_1_out, not_1_out, not_2_out);
  and and_2 (and_2_out, in_1, in_2);
  or or_1 (out_3, and_1_out, and_2_out);
endmodule

module Seg_Piso (
  input  A,
  input  B,
  input  C,
  input  D,
  output out_5
);

  wire and_1_out, and_2_out, and_3_out, and_4_out, and_5_out, and_6_out, not_1_out, not_2_out, not_3_out,
       not_4_out;

  not not_1 (not_1_out, A);
  not not_2 (not_2_out, B);
  not not_3 (not_3_out, C);
  not not_4 (not_4_out, D);
  and and_1 (and_1_out, A, B, not_3_out);
  and and_2 (and_2_out, not_1_out, not_2_out, C);
  and and_3 (and_3_out, B, not_3_out, D);
  and and_4 (and_4_out, not_2_out, not_3_out, not_4_out);
  and and_5 (and_5_out, B, C, not_4_out);
  and and_6 (and_6_out, A, not_2_out, D);
  or or_1 (out_5, and_1_out, and_2_out, and_3_out, and_4_out, and_5_out, and_6_out);
endmodule

module Seg_Teto (
  input  A,
  input  B,
  input  C,
  input  D,
  output out_5
);

  wire and_1_out, and_2_out, and_3_out, and_4_out, and_5_out, and_6_out, and_7_out, not_1_out, not_2_out,
       not_3_out, not_4_out;

  not not_1 (not_1_out, A);
  not not_2 (not_2_out, B);
  not not_3 (not_3_out, C);
  not not_4 (not_4_out, D);
  and and_1 (and_1_out, D, C, B);
  and and_2 (and_2_out, D, not_1_out, C);
  and and_3 (and_3_out, not_1_out, not_2_out, not_4_out);
  and and_4 (and_4_out, A, not_3_out, not_4_out);
  and and_5 (and_5_out, not_4_out, C);
  and and_6 (and_6_out, not_2_out, not_3_out, A);
  and and_7 (and_7_out, not_1_out, B, D);
  or or_1 (out_5, and_1_out, and_2_out, and_3_out, and_4_out, and_5_out, and_6_out, and_7_out);
endmodule

module Seg_Meio (
  input  A,
  input  B,
  input  C,
  input  D,
  output out_5
);

  wire and_1_out, and_2_out, and_3_out, and_4_out, and_5_out, not_1_out, not_2_out, not_3_out, not_4_out;

  not not_1 (not_1_out, A);
  not not_2 (not_2_out, B);
  not not_3 (not_3_out, C);
  not not_4 (not_4_out, D);
  and and_1 (and_1_out, A, not_2_out);
  and and_2 (and_2_out, not_3_out, B, not_1_out);
  and and_3 (and_3_out, not_1_out, not_2_out, C);
  and and_4 (and_4_out, C, not_4_out);
  and and_5 (and_5_out, A, B, D);
  or or_1 (out_5, and_1_out, and_2_out, and_3_out, and_4_out, and_5_out);
endmodule

module Seg_Dir_Baixo (
  input  A,
  input  B,
  input  C,
  input  D,
  output out_5
);

  wire and_1_out, and_2_out, and_3_out, and_4_out, and_5_out, not_1_out, not_2_out, not_3_out;

  not not_1 (not_1_out, A);
  not not_2 (not_2_out, B);
  not not_3 (not_3_out, C);
  and and_1 (and_1_out, not_1_out, B);
  and and_2 (and_2_out, not_1_out, not_2_out, not_3_out);
  and and_3 (and_3_out, not_2_out, A);
  and and_4 (and_4_out, not_3_out, D);
  and and_5 (and_5_out, not_1_out, C, D);
  or or_1 (out_5, and_1_out, and_2_out, and_3_out, and_4_out, and_5_out);
endmodule

module Seg_Esq_Baixo (
  input  A,
  input  B,
  input  C,
  input  D,
  output out_5
);

  wire and_1_out, and_2_out, and_3_out, and_4_out, not_2_out, not_3_out, not_4_out;

  // NOT_Gate not_1 has open pins: in=A, out=open
  not not_2 (not_2_out, B);
  not not_3 (not_3_out, C);
  not not_4 (not_4_out, D);
  and and_1 (and_1_out, A, not_2_out, C);
  and and_2 (and_2_out, A, B);
  and and_3 (and_3_out, not_2_out, not_3_out, not_4_out);
  and and_4 (and_4_out, C, not_4_out);
  or or_1 (out_5, and_1_out, and_2_out, and_3_out, and_4_out);
endmodule

module Seg_Dir_Cima (
  input  A,
  input  B,
  input  C,
  input  D,
  output out_5
);

  wire and_1_out, and_2_out, and_3_out, and_4_out, and_5_out, not_1_out, not_2_out, not_3_out, not_4_out;

  not not_1 (not_1_out, A);
  not not_2 (not_2_out, B);
  not not_3 (not_3_out, C);
  not not_4 (not_4_out, D);
  and and_1 (and_1_out, D, A, not_3_out);
  and and_2 (and_2_out, not_1_out, not_2_out);
  and and_3 (and_3_out, not_2_out, A, not_4_out);
  and and_4 (and_4_out, not_4_out, not_3_out, not_1_out);
  and and_5 (and_5_out, not_1_out, C, D);
  or or_1 (out_5, and_1_out, and_2_out, and_3_out, and_4_out, and_5_out);
endmodule

module Seg_Esq_Cima (
  input  A,
  input  B,
  input  C,
  input  D,
  output out_5
);

  wire and_1_out, and_2_out, and_3_out, and_4_out, and_5_out, not_1_out, not_2_out, not_3_out, not_4_out;

  not not_1 (not_1_out, A);
  not not_2 (not_2_out, B);
  not not_3 (not_3_out, C);
  not not_4 (not_4_out, D);
  and and_1 (and_1_out, A, not_2_out);
  and and_2 (and_2_out, not_1_out, B, not_3_out);
  and and_3 (and_3_out, B, not_4_out, C);
  and and_4 (and_4_out, not_3_out, not_4_out);
  and and_5 (and_5_out, A, B, C);
  or or_1 (out_5, and_1_out, and_2_out, and_3_out, and_4_out, and_5_out);
endmodule

module Mostrador (
  input  in_1,
  input  in_2,
  input  in_3,
  input  in_4,
  output out_5,
  output out_6,
  output out_7,
  output out_8,
  output out_9,
  output out_10,
  output out_11
);

  Seg_Meio seg_meio_1 (.A(in_1), .B(in_2), .C(in_3), .D(in_4), .out_5(out_5));
  Seg_Esq_Cima seg_esq_cima_1 (.A(in_1), .B(in_2), .C(in_3), .D(in_4), .out_5(out_6));
  Seg_Dir_Cima seg_dir_cima_1 (.A(in_1), .B(in_2), .C(in_3), .D(in_4), .out_5(out_8));
  Seg_Teto seg_teto_1 (.A(in_1), .B(in_2), .C(in_3), .D(in_4), .out_5(out_7));
  Seg_Dir_Baixo seg_dir_baixo_1 (.A(in_1), .B(in_2), .C(in_3), .D(in_4), .out_5(out_11));
  Seg_Piso seg_piso_1 (.A(in_1), .B(in_2), .C(in_3), .D(in_4), .out_5(out_10));
  Seg_Esq_Baixo seg_esq_baixo_1 (.A(in_1), .B(in_2), .C(in_3), .D(in_4), .out_5(out_9));
endmodule

module relojo6 (
  input  clk,
  input  f_18,
  input  in_3,
  input  [3:0] usu,
  input  \config ,
  output [3:0] out_6,
  output _0,
  output _6
);

  wire and_1_out, and_2_out, and_3_out, or_1_out;
  wire [3:0] com_bot_o_7b0cf85d_1_out_4, com_bot_o_7b0cf85d_2_out_4, subtractor_1_out, subtractor_2_out;

  com_bot_o_7b0cf85d com_bot_o_7b0cf85d_1 (
    .in_2(com_bot_o_7b0cf85d_2_out_4), .in_3(usu), .in_1(\config ), .out_4(com_bot_o_7b0cf85d_1_out_4));
  and and_1 (and_1_out, clk, ~and_2_out);  // AND_Gate
  and and_2 (and_2_out, f_18, in_3, _0);
  and and_3 (and_3_out, clk, \config );
  or or_1 (or_1_out, and_3_out, and_1_out);
  D_Flip_Flop d_ff_1 (.clk(or_1_out), .D(com_bot_o_7b0cf85d_1_out_4[0]), .Q(out_6[0]));  // open: Qn, preset, en, reset
  D_Flip_Flop d_ff_2 (.clk(or_1_out), .D(com_bot_o_7b0cf85d_1_out_4[1]), .Q(out_6[1]));  // open: Qn, preset, en, reset
  D_Flip_Flop d_ff_3 (.clk(or_1_out), .D(com_bot_o_7b0cf85d_1_out_4[2]), .Q(out_6[2]));  // open: Qn, preset, en, reset
  and and_4 (_6, out_6[2], ~out_6[1], out_6[0], ~com_bot_o_7b0cf85d_1_out_4[3]);  // AND_Gate
  D_Flip_Flop d_ff_4 (.clk(or_1_out), .D(com_bot_o_7b0cf85d_1_out_4[3]), .Q(out_6[3]));  // open: Qn, preset, en, reset
  and and_5 (_0, ~out_6[0], ~out_6[1], ~out_6[2]);  // AND_Gate
  com_bot_o_7b0cf85d com_bot_o_7b0cf85d_2 (
    .in_2(subtractor_2_out), .in_3(subtractor_1_out), .in_1(_0), .out_4(com_bot_o_7b0cf85d_2_out_4));
  Subtractor #(.width(4)) subtractor_1 (.a(out_6), .b(4'b1011), .out(subtractor_1_out));  // open: bin, bout
  Hex_Digit_Display hex_digit_display_1 (.value(out_6));  // open: dp
  Subtractor #(.width(4)) subtractor_2 (.a(out_6), .b(4'b0001), .out(subtractor_2_out));  // open: bin, bout
endmodule

module relogio_9 (
  input  clk,
  input  de_f,
  input  in_3,
  input  in_4,
  input  [3:0] usu,
  input  \config ,
  output [3:0] sai,
  output _0,
  output _9
);

  wire and_1_out, and_2_out, and_3_out, or_1_out;
  wire [3:0] com_bot_o_7b0cf85d_1_out_4, com_bot_o_7b0cf85d_2_out_4, subtractor_1_out, subtractor_2_out;

  and and_1 (and_1_out, clk, ~and_2_out);  // AND_Gate
  and and_2 (and_2_out, in_3, de_f, _0, in_4);
  com_bot_o_7b0cf85d com_bot_o_7b0cf85d_1 (
    .in_2(com_bot_o_7b0cf85d_2_out_4), .in_3(usu), .in_1(\config ), .out_4(com_bot_o_7b0cf85d_1_out_4));
  and and_3 (and_3_out, clk, \config );
  or or_1 (or_1_out, and_3_out, and_1_out);
  D_Flip_Flop d_ff_1 (.clk(or_1_out), .D(com_bot_o_7b0cf85d_1_out_4[0]), .Q(sai[0]));  // open: Qn, preset, en, reset
  D_Flip_Flop d_ff_2 (.clk(or_1_out), .D(com_bot_o_7b0cf85d_1_out_4[1]), .Q(sai[1]));  // open: Qn, preset, en, reset
  D_Flip_Flop d_ff_3 (.clk(or_1_out), .D(com_bot_o_7b0cf85d_1_out_4[2]), .Q(sai[2]));  // open: Qn, preset, en, reset
  and and_4 (_9, ~sai[1], sai[0], ~sai[2], sai[3]);  // AND_Gate
  D_Flip_Flop d_ff_4 (.clk(or_1_out), .D(com_bot_o_7b0cf85d_1_out_4[3]), .Q(sai[3]));  // open: Qn, preset, en, reset
  and and_5 (_0, ~sai[0], ~sai[2], ~sai[3], ~sai[1]);  // AND_Gate
  com_bot_o_7b0cf85d com_bot_o_7b0cf85d_2 (
    .in_2(subtractor_2_out), .in_3(subtractor_1_out), .in_1(_0), .out_4(com_bot_o_7b0cf85d_2_out_4));
  Subtractor #(.width(4)) subtractor_1 (.a(sai), .b(4'b0111), .out(subtractor_1_out));  // open: bin, bout
  Hex_Digit_Display hex_digit_display_1 (.value(sai));  // open: dp
  Subtractor #(.width(4)) subtractor_2 (.a(sai), .b(4'b0001), .out(subtractor_2_out));  // open: bin, bout
endmodule

module cot_9 (
  input  clk,
  output [3:0] out_2,
  output out_3
);

  wire and_1_out;
  wire [3:0] adder_1_out, adder_2_out, com_bot_o_7b0cf85d_1_out_4;

  D_Flip_Flop d_ff_1 (.clk(clk), .D(com_bot_o_7b0cf85d_1_out_4[0]), .Q(out_2[0]));  // open: Qn, preset, en, reset
  D_Flip_Flop d_ff_2 (.clk(clk), .D(com_bot_o_7b0cf85d_1_out_4[1]), .Q(out_2[1]));  // open: Qn, preset, en, reset
  D_Flip_Flop d_ff_3 (.clk(clk), .D(com_bot_o_7b0cf85d_1_out_4[2]), .Q(out_2[2]));  // open: Qn, preset, en, reset
  D_Flip_Flop d_ff_4 (.clk(clk), .D(com_bot_o_7b0cf85d_1_out_4[3]), .Q(out_2[3]));  // open: Qn, preset, en, reset
  and and_1 (and_1_out, out_2[0], ~out_2[2], out_2[3], ~out_2[1]);  // AND_Gate
  com_bot_o_7b0cf85d com_bot_o_7b0cf85d_1 (
    .in_2(adder_2_out), .in_3(adder_1_out), .in_1(and_1_out), .out_4(com_bot_o_7b0cf85d_1_out_4));
  Adder #(.width(4)) adder_1 (.a(out_2), .b(4'b0111), .out(adder_1_out));  // open: cin, cout
  and and_2 (out_3, ~out_2[0], ~out_2[3], ~out_2[2], ~out_2[1]);  // AND_Gate
  Hex_Digit_Display hex_digit_display_1 (.value(out_2));  // open: dp
  Adder #(.width(4)) adder_2 (.a(out_2), .b(4'b0001), .out(adder_2_out));  // open: cin, cout
endmodule

module cot_6 (
  input  clk,
  output [3:0] out_2,
  output out_3
);

  wire and_1_out;
  wire [3:0] adder_1_out, adder_2_out, com_bot_o_7b0cf85d_1_out_4;

  D_Flip_Flop d_ff_1 (.clk(clk), .D(com_bot_o_7b0cf85d_1_out_4[0]), .Q(out_2[0]));  // open: Qn, preset, en, reset
  D_Flip_Flop d_ff_2 (.clk(clk), .D(com_bot_o_7b0cf85d_1_out_4[1]), .Q(out_2[1]));  // open: Qn, preset, en, reset
  D_Flip_Flop d_ff_3 (.clk(clk), .D(com_bot_o_7b0cf85d_1_out_4[2]), .Q(out_2[2]));  // open: Qn, preset, en, reset
  D_Flip_Flop d_ff_4 (.clk(clk), .D(com_bot_o_7b0cf85d_1_out_4[3]), .Q(out_2[3]));  // open: Qn, preset, en, reset
  and and_1 (and_1_out, out_2[0], ~out_2[1], out_2[2]);  // AND_Gate
  com_bot_o_7b0cf85d com_bot_o_7b0cf85d_1 (
    .in_2(adder_2_out), .in_3(adder_1_out), .in_1(and_1_out), .out_4(com_bot_o_7b0cf85d_1_out_4));
  Adder #(.width(4)) adder_1 (.a(out_2), .b(4'b1011), .out(adder_1_out));  // open: cin, cout
  and and_2 (out_3, ~out_2[0], ~out_2[1], ~out_2[2]);  // AND_Gate
  Hex_Digit_Display hex_digit_display_1 (.value(out_2));  // open: dp
  Adder #(.width(4)) adder_2 (.a(out_2), .b(4'b0001), .out(adder_2_out));  // open: cin, cout
endmodule

module alavan (
  input  in_1,
  output out_2
);

  wire d_ff_1_q;

  D_Flip_Flop d_ff_1 (.clk(in_1), .D(out_2), .Q(d_ff_1_q));  // open: Qn, preset, en, reset
  not not_1 (out_2, d_ff_1_q);
endmodule

module rlogio_9_esp (
  input  clk,
  input  [3:0] usu,
  input  \config ,
  output [3:0] sai,
  output out_5,
  output out_6
);

  wire and_1_out, and_2_out, mine_easter_egg_out;
  wire [3:0] com_bot_o_7b0cf85d_1_out_4, com_bot_o_7b0cf85d_2_out_4, subtractor_1_out, subtractor_2_out;

  com_bot_o_7b0cf85d com_bot_o_7b0cf85d_1 (
    .in_2(com_bot_o_7b0cf85d_2_out_4), .in_3(usu), .in_1(\config ), .out_4(com_bot_o_7b0cf85d_1_out_4));
  and and_1 (and_1_out, clk, ~out_6);  // AND_Gate
  and and_2 (and_2_out, clk, \config );
  or mine_easter_egg (mine_easter_egg_out, and_1_out, and_2_out);
  D_Flip_Flop d_ff_1 (
    .clk(mine_easter_egg_out), .D(com_bot_o_7b0cf85d_1_out_4[0]), .Q(sai[0]));  // open: Qn, preset, en, reset
  D_Flip_Flop d_ff_2 (
    .clk(mine_easter_egg_out), .D(com_bot_o_7b0cf85d_1_out_4[1]), .Q(sai[1]));  // open: Qn, preset, en, reset
  D_Flip_Flop d_ff_3 (
    .clk(mine_easter_egg_out), .D(com_bot_o_7b0cf85d_1_out_4[2]), .Q(sai[2]));  // open: Qn, preset, en, reset
  and and_3 (out_6, ~sai[1], ~sai[0], ~sai[2], ~sai[3]);  // AND_Gate
  D_Flip_Flop d_ff_4 (
    .clk(mine_easter_egg_out), .D(com_bot_o_7b0cf85d_1_out_4[3]), .Q(sai[3]));  // open: Qn, preset, en, reset
  and and_4 (out_5, ~sai[0], ~sai[2], ~sai[3], ~sai[1]);  // AND_Gate
  com_bot_o_7b0cf85d com_bot_o_7b0cf85d_2 (
    .in_2(subtractor_2_out), .in_3(subtractor_1_out), .in_1(out_5), .out_4(com_bot_o_7b0cf85d_2_out_4));
  Subtractor #(.width(4)) subtractor_1 (.a(sai), .b(4'b0111), .out(subtractor_1_out));  // open: bin, bout
  Hex_Digit_Display hex_digit_display_1 (.value(sai));  // open: dp
  Subtractor #(.width(4)) subtractor_2 (.a(sai), .b(4'b0001), .out(subtractor_2_out));  // open: bin, bout
endmodule

module JJJJJ (
  input  in_1,
  input  in_2,
  input  in_3,
  input  in_4,
  output [3:0] out_5
);

  wire [3:0] not_1_out;

  not not_1 (not_1_out[0], in_1);
  not not_2 (not_1_out[1], in_2);
  not not_3 (not_1_out[2], in_3);
  not not_4 (not_1_out[3], in_4);
  Adder #(.width(4)) adder_1 (.a(4'b0001), .b(not_1_out), .out(out_5));  // open: cin, cout
endmodule

module TTTTT (
  input  [3:0] in_1,
  input  [3:0] in_2,
  input  [3:0] in_3,
  input  [3:0] in_4,
  output out_5
);

  wire or_1_out, or_2_out, or_3_out, or_4_out, or_5_out;

  or or_1 (or_1_out, in_1[3], in_1[2], in_1[1], in_1[0]);
  or or_2 (or_2_out, in_2[3], in_2[2], in_2[1], in_2[0]);
  or or_3 (or_3_out, or_1_out, or_2_out, or_4_out, or_5_out);
  or or_4 (or_4_out, in_3[3], in_3[2], in_3[1], in_3[0]);
  or or_5 (or_5_out, in_4[3], in_4[2], in_4[1], in_4[0]);
  not not_1 (out_5, or_3_out);
endmodule

module TESTE_1 (
  input  [3:0] in_1,
  output [3:0] out_2
);

  wire [3:0] jjjjj_1_out_5;

  JJJJJ jjjjj_1 (.in_1(in_1[0]), .in_2(in_1[1]), .in_3(in_1[2]), .in_4(in_1[3]), .out_5(jjjjj_1_out_5));
  com_bot_o_7b0cf85d com_bot_o_7b0cf85d_1 (.in_2(in_1), .in_3(jjjjj_1_out_5), .in_1(in_1[3]), .out_4(out_2));
endmodule

module Demultiplexador (
  input  [3:0] in_1,
  input  in_2,
  output [3:0] out_3,
  output [3:0] out_4
);

  SLSLS slsls_1 (.in_1(in_1[0]), .in_2(in_2), .out_3(out_4[0]), .out_4(out_3[0]));
  SLSLS slsls_2 (.in_1(in_1[1]), .in_2(in_2), .out_3(out_4[1]), .out_4(out_3[1]));
  SLSLS slsls_3 (.in_1(in_1[2]), .in_2(in_2), .out_3(out_4[2]), .out_4(out_3[2]));
  SLSLS slsls_4 (.in_1(in_1[3]), .in_2(in_2), .out_3(out_4[3]), .out_4(out_3[3]));
endmodule

module SLSLS (
  input  in_1,
  input  in_2,
  output out_3,
  output out_4
);

  and and_1 (out_3, in_1, ~in_2);  // AND_Gate
  and and_2 (out_4, in_2, in_1);
endmodule

module KKKKK (
  input  in_1,
  input  in_2,
  input  in_3,
  input  in_4,
  input  in_5,
  input  in_6,
  output [3:0] out_7,
  output [3:0] out_8,
  output out_9,
  output out_10,
  output [3:0] out_11,
  output [3:0] out_12
);

  wire alavan_1_out_2, not_1_out, not_2_out, slsls_1_out_3, slsls_1_out_4;

  LED led_1 (.in(in_3));
  Hex_Digit_Display hex_digit_display_1 (.value(out_11));  // open: dp
  TESTE_1 teste_1_1 (.in_1(out_7), .out_2(out_11));
  YAYA yaya_1 (.in_2(alavan_1_out_2), .in_1({in_3, in_4, in_5, in_6}), .in_3(in_1), .out_4(out_7));
  D_Flip_Flop d_ff_1 (.clk(alavan_1_out_2), .D(slsls_1_out_3), .Q(out_9), .reset(in_1));  // open: Qn, preset, en
  not not_1 (not_1_out, alavan_1_out_2);
  SLSLS slsls_1 (.in_1(in_3), .in_2(alavan_1_out_2), .out_3(slsls_1_out_3), .out_4(slsls_1_out_4));
  TESTE_1 teste_1_2 (.in_1(out_8), .out_2(out_12));
  YAYA yaya_2 (.in_2(not_2_out), .in_1({in_3, in_4, in_5, in_6}), .in_3(in_1), .out_4(out_8));
  not not_2 (not_2_out, alavan_1_out_2);
  D_Flip_Flop d_ff_2 (.clk(not_1_out), .D(slsls_1_out_4), .Q(out_10), .reset(in_1));  // open: Qn, preset, en
  alavan alavan_1 (.in_1(in_2), .out_2(alavan_1_out_2));
  Hex_Digit_Display hex_digit_display_2 (.value(out_12));  // open: dp
endmodule

module YAYA (
  input  [3:0] in_1,
  input  in_2,
  input  in_3,
  output [3:0] out_4
);

  D_Flip_Flop d_ff_1 (.clk(in_2), .D(in_1[3]), .Q(out_4[3]), .reset(in_3));  // open: Qn, preset, en
  D_Flip_Flop d_ff_2 (.clk(in_2), .D(in_1[2]), .Q(out_4[2]), .reset(in_3));  // open: Qn, preset, en
  D_Flip_Flop d_ff_3 (.clk(in_2), .D(in_1[1]), .Q(out_4[1]), .reset(in_3));  // open: Qn, preset, en
  D_Flip_Flop d_ff_4 (.clk(in_2), .D(in_1[0]), .Q(out_4[0]), .reset(in_3));  // open: Qn, preset, en
endmodule

module MAOISOI (
  input  [3:0] Entrada_A,
  input  [3:0] Entrada_B,
  input  Tempo_zerado,
  input  Chute,
  input  in_5,
  output \Posição_X ,
  output \Posição_Y ,
  output Neg_A,
  output [3:0] Saida_A,
  output Neg_B,
  output [3:0] Saida_B,
  output [3:0] out_12,
  output [3:0] out_13,
  output A_Jogando,
  output B_Jogando
);

  wire d_ff_5_q, iguais_1_out_3, iguais_2_out_3, iguais_3_out_3, not_4_out, not_5_out, or_1_out,
       triangulo_1_out_4;
  wire [3:0] adder_1_out, com_bot_o_7b0cf85d_1_out_4, com_bot_o_7b0cf85d_2_out_4, d_ff_1_q;

  D_Flip_Flop d_ff_1 (
    .clk(Chute), .D(com_bot_o_7b0cf85d_2_out_4[0]), .Q(d_ff_1_q[0]), .reset(in_5));  // open: Qn, preset, en
  not not_1 (B_Jogando, A_Jogando);
  com_bot_o_7b0cf85d com_bot_o_7b0cf85d_1 (
    .in_2(Entrada_B), .in_3(Entrada_A), .in_1(A_Jogando), .out_4(com_bot_o_7b0cf85d_1_out_4));
  D_Flip_Flop d_ff_2 (
    .clk(Chute), .D(com_bot_o_7b0cf85d_2_out_4[1]), .Q(d_ff_1_q[1]), .reset(in_5));  // open: Qn, preset, en
  not not_2 (\Posição_Y , \Posição_X );
  KKKKK kkkkk_1 (
    .out_9(Neg_B), .out_11(Saida_B), .out_12(Saida_A), .in_3(com_bot_o_7b0cf85d_1_out_4[3]),
    .in_4(com_bot_o_7b0cf85d_1_out_4[2]), .in_5(com_bot_o_7b0cf85d_1_out_4[1]),
    .in_6(com_bot_o_7b0cf85d_1_out_4[0]), .out_10(Neg_A), .in_2(Chute), .out_7(out_12), .out_8(out_13),
    .in_1(in_5));
  D_Flip_Flop d_ff_3 (
    .clk(Chute), .D(com_bot_o_7b0cf85d_2_out_4[2]), .Q(d_ff_1_q[2]), .reset(in_5));  // open: Qn, preset, en
  alavan alavan_1 (.in_1(Chute), .out_2(\Posição_X ));
  iguais iguais_1 (.in_1(d_ff_1_q), .in_2(4'b0000), .out_3(iguais_1_out_3));
  D_Flip_Flop d_ff_4 (
    .clk(Chute), .D(com_bot_o_7b0cf85d_2_out_4[3]), .Q(d_ff_1_q[3]), .reset(in_5));  // open: Qn, preset, en
  not not_3 (A_Jogando, triangulo_1_out_4);
  or or_1 (or_1_out, iguais_1_out_3, iguais_2_out_3);
  not not_4 (not_4_out, Tempo_zerado);
  iguais iguais_2 (.in_1(d_ff_1_q), .in_2(4'b0001), .out_3(iguais_2_out_3));
  Adder #(.width(4)) adder_1 (.a(d_ff_1_q), .b(4'b0001), .out(adder_1_out));  // open: cin, cout
  iguais iguais_3 (.in_1(adder_1_out), .in_2(4'b0100), .out_3(iguais_3_out_3));
  triangulo triangulo_1 (.in_2(not_5_out), .in_3(d_ff_5_q), .in_1(Tempo_zerado), .out_4(triangulo_1_out_4));
  not not_5 (not_5_out, d_ff_5_q);
  com_bot_o_7b0cf85d com_bot_o_7b0cf85d_2 (
    .in_2(adder_1_out), .in_3(4'b0000), .in_1(iguais_3_out_3), .out_4(com_bot_o_7b0cf85d_2_out_4));
  D_Flip_Flop #(.trigger("high")) d_ff_5 (.clk(not_4_out), .D(or_1_out), .Q(d_ff_5_q));  // open: Qn, preset, en, reset
endmodule

module iguais (
  input  [3:0] in_1,
  input  [3:0] in_2,
  output out_3
);

  wire xnor_1_out, xnor_2_out, xnor_3_out, xnor_4_out;

  xnor xnor_1 (xnor_1_out, in_1[0], in_2[0]);
  xnor xnor_2 (xnor_2_out, in_1[1], in_2[1]);
  xnor xnor_3 (xnor_3_out, in_1[2], in_2[2]);
  xnor xnor_4 (xnor_4_out, in_2[3], in_1[3]);
  and and_1 (out_3, xnor_1_out, xnor_2_out, xnor_3_out, xnor_4_out);
endmodule

module TESTANDO_1_2_3 (
  input  Calcular_resultdo,
  input  Tempo_esgotado,
  input  Chutar,
  input  in_4,
  input  in_5,
  input  in_6,
  input  in_7,
  input  in_8,
  input  in_9,
  input  in_10,
  input  in_11,
  input  Resetar,
  output Chutando_X,
  output Chutando_Y,
  output Neg_X,
  output Neg_Y,
  output [3:0] \Posição_X ,
  output [3:0] \Posição_Y ,
  output Neg_A,
  output [3:0] Chute_A,
  output Neg_B,
  output [3:0] Chute_B,
  output [3:0] \Pontuação_A ,
  output [3:0] \Pontuação_B ,
  output A_jogando,
  output B_jogando,
  output Maior,
  output Igual,
  output Menor,
  output Acertou
);

  wire comparar_1_out_9, or_1_out;
  wire [3:0] maoisoi_1_out_12, maoisoi_1_out_13;

  TESTE_1 teste_1_1 (.in_1({in_4, in_5, in_6, in_7}), .out_2(Chute_A));
  MAOISOI maoisoi_1 (
    .out_12(maoisoi_1_out_12), .A_Jogando(A_jogando), .Entrada_A({in_4, in_5, in_6, in_7}),
    .B_Jogando(B_jogando), .Entrada_B({in_8, in_9, in_10, in_11}), .out_13(maoisoi_1_out_13), .Neg_A(Neg_X),
    .\Posição_X (Chutando_X), .Saida_A(\Posição_X ), .Neg_B(Neg_Y), .\Posição_Y (Chutando_Y),
    .Saida_B(\Posição_Y ), .Chute(Chutar), .Tempo_zerado(Tempo_esgotado), .in_5(Resetar));
  or or_1 (or_1_out, Resetar, comparar_1_out_9);
  TESTE_1 teste_1_2 (.in_1({in_8, in_9, in_10, in_11}), .out_2(Chute_B));
  Comparar comparar_1 (
    .in_3(maoisoi_1_out_13), .in_4(maoisoi_1_out_12), .out_5(Maior), .out_6(Igual), .in_1(Calcular_resultdo),
    .out_8(Menor), .out_7(Acertou), .in_2(or_1_out), .out_9(comparar_1_out_9));
  Placar placar_1 (
    .out_6(\Pontuação_A ), .in_3(Acertou), .in_4(comparar_1_out_9), .in_5(Tempo_esgotado),
    .out_7(\Pontuação_B ), .in_1(A_jogando), .in_2(Resetar));

  assign Neg_A = in_4;
  assign Neg_B = in_8;
endmodule

module Comparador_2 (
  input  [3:0] in_1,
  input  [3:0] in_2,
  output out_3,
  output out_4,
  output out_5
);

  wire l_00_ou_11_2cab960a_1_out_3, l_00_ou_11_2cab960a_2_out_3, l_00_ou_11_2cab960a_3_out_3,
       l_00_ou_11_2cab960a_4_out_3, L_3e218025_2_out, L_3e218025_3_out, L_3e218025_4_out, L_3e218025_out,
       l_6af18fe5_1_out_4, l_6af18fe5_2_out_4, l_6af18fe5_3_out_4, l_6af18fe5_4_out_4, l_19270569_1_out_3,
       l_19270569_1_out_4, l_19270569_2_out_3, l_19270569_2_out_4, l_19270569_3_out_3, l_19270569_3_out_4,
       l_19270569_4_out_3, l_19270569_4_out_4, L_bb417b61_2_out, L_bb417b61_3_out, L_bb417b61_4_out,
       L_bb417b61_out, mine_2_out, mine_out, mostrador_1_out_5, mostrador_1_out_6, mostrador_1_out_7,
       mostrador_1_out_8, mostrador_1_out_9, mostrador_1_out_10, mostrador_1_out_11;

  _7_Segment_Display u_7_segment_display_1 (
    .g(mostrador_1_out_8), .f(mostrador_1_out_7), .a(mostrador_1_out_6), .b(mostrador_1_out_5),
    .e(mostrador_1_out_11), .d(mostrador_1_out_10), .c(mostrador_1_out_9));  // open: dp
  Mostrador mostrador_1 (
    .in_1(in_2[3]), .in_2(in_2[2]), .in_3(in_2[1]), .in_4(in_2[0]), .out_9(mostrador_1_out_9),
    .out_10(mostrador_1_out_10), .out_11(mostrador_1_out_11), .out_5(mostrador_1_out_5),
    .out_6(mostrador_1_out_6), .out_7(mostrador_1_out_7), .out_8(mostrador_1_out_8));
  L_19270569 l_19270569_1 (.in_1(in_1[2]), .in_2(in_2[2]), .out_3(l_19270569_1_out_3), .out_4(l_19270569_1_out_4));
  L_19270569 l_19270569_2 (.in_1(in_1[0]), .in_2(in_2[0]), .out_3(l_19270569_2_out_3), .out_4(l_19270569_2_out_4));
  L_00_ou_11_2cab960a l_00_ou_11_2cab960a_1 (.in_1(in_1[0]), .in_2(in_2[0]), .out_3(l_00_ou_11_2cab960a_1_out_3));
  L_00_ou_11_2cab960a l_00_ou_11_2cab960a_2 (.in_1(in_2[1]), .in_2(in_1[1]), .out_3(l_00_ou_11_2cab960a_2_out_3));
  L_00_ou_11_2cab960a l_00_ou_11_2cab960a_3 (.in_1(in_1[2]), .in_2(in_2[2]), .out_3(l_00_ou_11_2cab960a_3_out_3));
  L_00_ou_11_2cab960a l_00_ou_11_2cab960a_4 (.in_1(in_1[3]), .in_2(in_2[3]), .out_3(l_00_ou_11_2cab960a_4_out_3));
  L_19270569 l_19270569_3 (.in_1(in_1[3]), .in_2(in_2[3]), .out_3(l_19270569_3_out_3), .out_4(l_19270569_3_out_4));
  L_19270569 l_19270569_4 (.in_1(in_1[1]), .in_2(in_2[1]), .out_3(l_19270569_4_out_3), .out_4(l_19270569_4_out_4));
  and and_1 (out_3, l_00_ou_11_2cab960a_1_out_3, l_00_ou_11_2cab960a_2_out_3, l_00_ou_11_2cab960a_3_out_3, l_00_ou_11_2cab960a_4_out_3);
  L_6af18fe5 l_6af18fe5_1 (
    .in_2(l_19270569_3_out_3), .in_3(l_19270569_3_out_4), .in_1(out_3), .out_4(l_6af18fe5_1_out_4));
  L_6af18fe5 l_6af18fe5_2 (
    .in_2(l_19270569_1_out_3), .in_3(l_19270569_1_out_4), .in_1(l_6af18fe5_1_out_4),
    .out_4(l_6af18fe5_2_out_4));
  or mine (mine_out, l_6af18fe5_1_out_4, l_6af18fe5_2_out_4);
  or mine_2 (mine_2_out, mine_out, l_6af18fe5_3_out_4);
  L_6af18fe5 l_6af18fe5_3 (
    .in_2(l_19270569_4_out_3), .in_3(l_19270569_4_out_4), .in_1(mine_out), .out_4(l_6af18fe5_3_out_4));
  L_6af18fe5 l_6af18fe5_4 (
    .in_2(l_19270569_2_out_3), .in_3(l_19270569_2_out_4), .in_1(mine_2_out), .out_4(l_6af18fe5_4_out_4));
  and L_3e218025 (L_3e218025_out, l_19270569_3_out_3, l_6af18fe5_1_out_4);
  and L_bb417b61 (L_bb417b61_out, l_6af18fe5_1_out_4, l_19270569_3_out_4);
  and L_3e218025_2 (L_3e218025_2_out, l_19270569_1_out_3, l_6af18fe5_2_out_4);
  and L_bb417b61_2 (L_bb417b61_2_out, l_6af18fe5_2_out_4, l_19270569_1_out_4);
  and L_3e218025_3 (L_3e218025_3_out, l_19270569_4_out_3, l_6af18fe5_3_out_4);
  and L_bb417b61_3 (L_bb417b61_3_out, l_6af18fe5_3_out_4, l_19270569_4_out_4);
  and L_3e218025_4 (L_3e218025_4_out, l_19270569_2_out_3, l_6af18fe5_4_out_4);
  and L_bb417b61_4 (L_bb417b61_4_out, l_6af18fe5_4_out_4, l_19270569_2_out_4);
  or L_3e218025_5 (out_4, L_3e218025_out, L_3e218025_2_out, L_3e218025_3_out, L_3e218025_4_out);
  or L_bb417b61_5 (out_5, L_bb417b61_out, L_bb417b61_2_out, L_bb417b61_3_out, L_bb417b61_4_out);
endmodule

module Comparar (
  input  in_1,
  input  in_2,
  input  [3:0] in_3,
  input  [3:0] in_4,
  output out_5,
  output out_6,
  output out_7,
  output out_8,
  output out_9
);

  wire and_1_out, and_2_out, comparador_2_1_out_3, comparador_2_1_out_4, comparador_2_1_out_5,
       iguais_1_out_3, iguais_2_out_3;
  wire [3:0] adder_1_out, adder_2_out, random_1_out, random_2_out, teste_1_1_out_2, teste_1_2_out_2,
       teste_1_3_out_2, teste_1_4_out_2;

  Random #(.width(4)) random_1 (.clk(in_2), .out(random_1_out));  // open: next, clr
  Random #(.width(4), .seed(7)) random_2 (.clk(in_2), .out(random_2_out));  // open: next, clr
  TESTE_1 teste_1_1 (.in_1(random_1_out), .out_2(teste_1_1_out_2));
  TESTE_1 teste_1_2 (.in_1(random_2_out), .out_2(teste_1_2_out_2));
  Hex_Digit_Display hex_digit_display_1 (.value(teste_1_2_out_2));  // open: dp
  Hex_Digit_Display hex_digit_display_2 (.value(teste_1_1_out_2));  // open: dp
  TESTE_1 teste_1_3 (.in_1(in_3), .out_2(teste_1_3_out_2));
  TESTE_1 teste_1_4 (.in_1(in_4), .out_2(teste_1_4_out_2));
  Adder #(.width(4)) adder_1 (.a(teste_1_1_out_2), .b(teste_1_2_out_2), .out(adder_1_out));  // open: cin, cout
  Comparador_2 comparador_2_1 (
    .in_1(adder_2_out), .in_2(adder_1_out), .out_3(comparador_2_1_out_3), .out_4(comparador_2_1_out_4),
    .out_5(comparador_2_1_out_5));
  Adder #(.width(4)) adder_2 (.a(teste_1_3_out_2), .b(teste_1_4_out_2), .out(adder_2_out));  // open: cin, cout
  D_Flip_Flop d_ff_1 (.clk(in_1), .D(comparador_2_1_out_4), .Q(out_5));  // open: Qn, preset, en, reset
  D_Flip_Flop d_ff_2 (.clk(in_1), .D(comparador_2_1_out_5), .Q(out_8));  // open: Qn, preset, en, reset
  D_Flip_Flop d_ff_3 (.clk(in_1), .D(comparador_2_1_out_3), .Q(out_6));  // open: Qn, preset, en, reset
  iguais iguais_1 (.in_1(teste_1_3_out_2), .in_2(teste_1_1_out_2), .out_3(iguais_1_out_3));
  iguais iguais_2 (.in_1(teste_1_4_out_2), .in_2(teste_1_2_out_2), .out_3(iguais_2_out_3));
  and and_1 (and_1_out, iguais_1_out_3, iguais_2_out_3);
  and and_2 (and_2_out, comparador_2_1_out_3, and_1_out);
  D_Flip_Flop d_ff_4 (.clk(in_1), .D(and_2_out), .Q(out_7));  // open: Qn, preset, en, reset
  and and_3 (out_9, and_2_out, in_1);
endmodule

module Placar (
  input  in_1,
  input  in_2,
  input  in_3,
  input  in_4,
  input  in_5,
  output [3:0] out_6,
  output [3:0] out_7
);

  wire and_1_out, not_1_out, not_2_out, slsls_1_out_3, slsls_1_out_4, triangulo_1_out_4;
  wire [3:0] adder_1_out, adder_2_out;

  Hex_Digit_Display hex_digit_display_1 (.value(out_6));  // open: dp
  YAYA yaya_1 (.in_2(slsls_1_out_4), .in_1(adder_1_out), .in_3(in_1), .out_4(out_6));
  Adder #(.width(4)) adder_1 (.a(4'b0001), .b(out_6), .out(adder_1_out));  // open: cin, cout
  SLSLS slsls_1 (.in_1(and_1_out), .in_2(triangulo_1_out_4), .out_3(slsls_1_out_3), .out_4(slsls_1_out_4));
  and and_1 (and_1_out, in_3, in_4);
  Hex_Digit_Display hex_digit_display_2 (.value(out_7));  // open: dp
  YAYA yaya_2 (.in_2(slsls_1_out_3), .in_1(adder_2_out), .in_3(in_1), .out_4(out_7));
  Adder #(.width(4)) adder_2 (.a(4'b0001), .b(out_7), .out(adder_2_out));  // open: cin, cout
  triangulo triangulo_1 (.in_2(in_2), .in_3(not_2_out), .in_1(not_1_out), .out_4(triangulo_1_out_4));
  not not_1 (not_1_out, in_5);
  not not_2 (not_2_out, in_2);
endmodule

module Acabou (
  input  Tempo_A,
  input  Tempo_B,
  input  [3:0] \Pontuação_A ,
  input  [3:0] \Pontuação_B ,
  output A_venceu,
  output Empate,
  output B_venceu,
  output Acabou
);

  wire and_1_out, comparador_2_1_out_3, comparador_2_1_out_4, iguais_1_out_3, iguais_2_out_3, or_1_out,
       slsls_1_out_3, slsls_1_out_4, xnor_1_out, xnor_2_out;

  xnor xnor_1 (xnor_1_out, 1'b1, Tempo_A);
  xnor xnor_2 (xnor_2_out, Tempo_A, Tempo_B);
  iguais iguais_1 (.in_1(\Pontuação_A ), .in_2(4'b1111), .out_3(iguais_1_out_3));
  iguais iguais_2 (.in_1(4'b1111), .in_2(\Pontuação_B ), .out_3(iguais_2_out_3));
  or or_1 (or_1_out, iguais_1_out_3, iguais_2_out_3);
  and and_1 (and_1_out, xnor_1_out, xnor_2_out);
  Comparador_2 comparador_2_1 (
    .in_1(\Pontuação_A ), .in_2(\Pontuação_B ), .out_3(comparador_2_1_out_3), .out_4(comparador_2_1_out_4));  // open: out_5
  or or_2 (Acabou, and_1_out, or_1_out);
  SLSLS slsls_1 (.in_1(Acabou), .in_2(comparador_2_1_out_4), .out_3(slsls_1_out_3), .out_4(slsls_1_out_4));
  triangulo triangulo_1 (.in_2(slsls_1_out_4), .in_3(1'b0), .in_1(comparador_2_1_out_3), .out_4(A_venceu));
  triangulo triangulo_2 (.in_2(slsls_1_out_3), .in_3(1'b0), .in_1(comparador_2_1_out_3), .out_4(B_venceu));
  and and_2 (Empate, comparador_2_1_out_3, Acabou);
endmodule

module SUSUASU (
  input  in_1,
  input  in_2,
  input  in_3,
  input  in_4,
  input  in_5,
  input  in_6,
  input  in_7,
  input  in_8
);

  wire A_jogando, A_venceu, Acertou, alavan_1_out_2, alavan_2_out_2, and_1_out, and_2_out, and_3_out,
       and_4_out, and_5_out, and_6_out, and_7_out, and_8_out, and_9_out, and_10_out, and_11_out, and_12_out,
       B_jogando, B_venceu, Calcular, Chutando_X, Chutando_Y, Chutar, clock_1_out, Configurar, dm_t, ds_t,
       Empate, Fim_de_jogo, Igual, ligar, Maior, Menor, not_3_out, or_1_out, Reset, reset_1_out_3, SA, SB,
       Start, SX, SY, TA, TB, tunnel, um_t, us_t, xor_1_out, xor_2_out;
  wire [3:0] DM, DMA, DMB, DS, DSA, DSB, GA, GB, PA, PB, UM, UMA, UMB, US, USA, USB, XH, YH;

  Hex_Digit_Display hex_digit_display_1 (.value(DMA));  // open: dp
  and and_1 (and_1_out, in_1, ligar);
  Hex_Digit_Display hex_digit_display_2 (.value(PA));  // open: dp
  LED led_1 (.in(1'b1));
  LED led_2 (.in(1'b1));
  Hex_Digit_Display hex_digit_display_3 (.value(UMA));  // open: dp
  LED led_3 (.in(SA));
  Hex_Digit_Display hex_digit_display_4 (.value(GA));  // open: dp
  LED led_4 (.in(A_jogando));
  and and_2 (and_2_out, in_2, ligar);
  and and_3 (and_3_out, in_3, ligar);
  Hex_Digit_Display hex_digit_display_5 (.value(USA));  // open: dp
  Hex_Digit_Display hex_digit_display_6 (.value(DSA));  // open: dp
  and and_4 (and_4_out, in_4, ligar);
  and and_5 (and_5_out, in_5, ligar);
  TESTANDO_1_2_3 testando_1_2_3_1 (
    .Calcular_resultdo(and_9_out), .A_jogando(A_jogando), .Tempo_esgotado(xor_1_out), .B_jogando(B_jogando),
    .Maior(Maior), .Igual(Igual), .Menor(Menor), .Acertou(Acertou), .Neg_A(SA), .Chute_A(GA), .Neg_X(SX),
    .\Posição_X (XH), .Chutando_X(Chutando_X), .Neg_Y(SY), .\Posição_Y (YH), .Chutando_Y(Chutando_Y),
    .Neg_B(SB), .Chute_B(GB), .\Pontuação_A (PA), .\Pontuação_B (PB), .in_4(and_1_out), .in_5(and_2_out),
    .in_6(and_3_out), .in_7(and_4_out), .Chutar(and_6_out), .in_8(and_5_out), .Resetar(Reset),
    .in_9(and_7_out), .in_10(and_8_out), .in_11(and_10_out));
  and and_6 (and_6_out, ligar, Chutar);
  and and_7 (and_7_out, in_6, ligar);
  and and_8 (and_8_out, in_7, ligar);
  and and_9 (and_9_out, ligar, Calcular);
  and and_10 (and_10_out, in_8, ligar);
  LED led_5 (.in(A_venceu));
  Button button_1 (.out(Start));
  Button button_2 (.out(dm_t));
  Hex_Digit_Display hex_digit_display_7 (.value(DM));  // open: dp
  LED led_6 (.in(Maior));
  LED led_7 (.in(SX));
  xor xor_1 (xor_1_out, TA, TB);
  LED led_8 (.in(Fim_de_jogo));
  LED led_9 (.in(Empate));
  LED led_10 (.in(tunnel));
  Button button_3 (.out(Configurar));
  Button button_4 (.out(um_t));
  LED led_11 (.in(1'b1));
  LED led_12 (.in(1'b1));
  Hex_Digit_Display hex_digit_display_8 (.value(UM));  // open: dp
  LED led_13 (.in(Acertou));
  LED led_14 (.in(Igual));
  Button button_5 (.out(Chutar));
  Hex_Digit_Display hex_digit_display_9 (.value(XH));  // open: dp
  LED led_15 (.in(Chutando_X));
  Button button_6 (.out(ds_t));
  Hex_Digit_Display hex_digit_display_10 (.value(DS));  // open: dp
  Hex_Digit_Display hex_digit_display_11 (.value(US));  // open: dp
  Button button_7 (.out(Calcular));
  LED led_16 (.in(SY));
  Hex_Digit_Display hex_digit_display_12 (.value(YH));  // open: dp
  LED led_17 (.in(Chutando_Y));
  alavan alavan_1 (.in_1(xor_2_out), .out_2(alavan_1_out_2));
  xor xor_2 (xor_2_out, Start, Reset);
  LED led_18 (.in(B_venceu));
  Button button_8 (.out(Reset));
  Button button_9 (.out(us_t));
  LED led_19 (.in(Menor));
  not not_1 (ligar, alavan_1_out_2);
  not not_2 (tunnel, alavan_2_out_2);
  alavan alavan_2 (.in_1(Configurar), .out_2(alavan_2_out_2));
  Clock clock_1 (.out(clock_1_out));
  crono crono_1 (
    .out_8(DMA), .out_9(UMA), .out_10(DSA), .out_11(USA), .in_1(and_11_out), .in_7(or_1_out), .out_12(TA),
    .in_2(DM), .in_3(UM), .in_4(DS), .in_5(US), .in_6(clock_1_out));
  and and_11 (and_11_out, A_jogando, ligar);
  reset reset_1 (.in_1(clock_1_out), .in_2(Reset), .out_3(reset_1_out_3));
  Hex_Digit_Display hex_digit_display_13 (.value(DMB));  // open: dp
  Hex_Digit_Display hex_digit_display_14 (.value(UMB));  // open: dp
  LED led_20 (.in(SB));
  or or_1 (or_1_out, tunnel, reset_1_out_3);
  Hex_Digit_Display hex_digit_display_15 (.value(PB));  // open: dp
  LED led_21 (.in(1'b1));
  LED led_22 (.in(1'b1));
  Hex_Digit_Display hex_digit_display_16 (.value(DSB));  // open: dp
  Hex_Digit_Display hex_digit_display_17 (.value(GB));  // open: dp
  LED led_23 (.in(B_jogando));
  and and_12 (and_12_out, not_3_out, ligar);
  not not_3 (not_3_out, and_11_out);
  Hex_Digit_Display hex_digit_display_18 (.value(USB));  // open: dp
  confr confr_1 (.in_2(dm_t), .in_3(um_t), .in_4(ds_t), .in_1(us_t), .out_5(DM), .out_6(UM), .out_7(DS), .out_8(US));
  crono crono_2 (
    .out_8(DMB), .out_9(UMB), .out_10(DSB), .out_11(USB), .in_1(and_12_out), .in_7(or_1_out), .out_12(TB),
    .in_2(DM), .in_3(UM), .in_4(DS), .in_5(US), .in_6(clock_1_out));
  Acabou acabou_1 (
    .Tempo_A(TA), .Tempo_B(TB), .\Pontuação_A (PA), .\Pontuação_B (PB), .A_venceu(A_venceu), .Empate(Empate),
    .B_venceu(B_venceu), .Acabou(Fim_de_jogo));

  // Other names for the same wires on the sheet: A0 = in_4; A1 = in_3; A2 = in_2; A3 = in_1; B0 = in_8; B1 = in_7;
  //   B2 = in_6; B3 = in_5
endmodule

module confr (
  input  in_1,
  input  in_2,
  input  in_3,
  input  in_4,
  output [3:0] out_5,
  output [3:0] out_6,
  output [3:0] out_7,
  output [3:0] out_8
);

  wire c6_out_3, c9_2_out_3, c9_3_out_3, xor_1_out, xor_2_out, xor_3_out;

  cot_9 c9 (.clk(xor_1_out), .out_2(out_5));  // open: out_3
  xor xor_1 (xor_1_out, in_2, c9_2_out_3);
  cot_9 c9_2 (.clk(xor_2_out), .out_2(out_6), .out_3(c9_2_out_3));
  xor xor_2 (xor_2_out, in_3, c6_out_3);
  cot_6 c6 (.clk(xor_3_out), .out_2(out_7), .out_3(c6_out_3));
  xor xor_3 (xor_3_out, in_4, c9_3_out_3);
  cot_9 c9_3 (.clk(in_1), .out_2(out_8), .out_3(c9_3_out_3));
endmodule

module crono (
  input  in_1,
  input  [3:0] in_2,
  input  [3:0] in_3,
  input  [3:0] in_4,
  input  [3:0] in_5,
  input  in_6,
  input  in_7,
  output [3:0] out_8,
  output [3:0] out_9,
  output [3:0] out_10,
  output [3:0] out_11,
  output out_12
);

  wire and_1_out, and_2_out, or_1_out, or_2_out, or_3_out, or_4_out, relogio_9_1__0, relogio_9_1__9,
       relogio_9_2__9, relojo6_1__0, relojo6_1__6, rlogio_9_esp_1_out_5, rlogio_9_esp_1_out_6;

  or or_1 (or_1_out, relogio_9_1__9, and_1_out);
  rlogio_9_esp rlogio_9_esp_1 (
    .clk(or_1_out), .out_5(rlogio_9_esp_1_out_5), .\config (in_7), .out_6(rlogio_9_esp_1_out_6), .sai(out_8),
    .usu(in_2));
  Hex_Digit_Display hex_digit_display_1 (.value(out_8));  // open: dp
  or or_2 (or_2_out, and_1_out, relojo6_1__6);
  or or_3 (or_3_out, relogio_9_2__9, and_1_out);
  relogio_9 relogio_9_1 (
    .clk(or_2_out), .in_3(rlogio_9_esp_1_out_6), .in_4(rlogio_9_esp_1_out_5), .sai(out_9),
    ._0(relogio_9_1__0), .usu(in_3), .\config (in_7), ._9(relogio_9_1__9));  // open: de_f
  Hex_Digit_Display hex_digit_display_2 (.value(out_9));  // open: dp
  or or_4 (or_4_out, and_2_out, and_1_out);
  relojo6 relojo6_1 (
    .clk(or_3_out), .f_18(relogio_9_1__0), .in_3(rlogio_9_esp_1_out_6), .\config (in_7), ._6(relojo6_1__6),
    .out_6(out_10), .usu(in_4), ._0(relojo6_1__0));
  Hex_Digit_Display hex_digit_display_3 (.value(out_10));  // open: dp
  TTTTT ttttt_1 (.in_1(out_8), .in_2(out_9), .in_3(out_10), .in_4(out_11), .out_5(out_12));
  and and_1 (and_1_out, in_6, in_7);
  relogio_9 relogio_9_2 (
    .clk(or_4_out), .de_f(relojo6_1__0), .in_3(relogio_9_1__0), .in_4(rlogio_9_esp_1_out_6), .sai(out_11),
    .usu(in_5), .\config (in_7), ._9(relogio_9_2__9));  // open: _0
  Hex_Digit_Display hex_digit_display_4 (.value(out_11));  // open: dp
  and and_2 (and_2_out, in_1, in_6);
endmodule

module FODASE (
  input  in_1,
  input  in_2,
  input  in_3,
  input  in_4,
  input  in_5,
  input  in_6,
  input  in_7,
  input  in_8,
  output out_9,
  output out_10,
  output out_11,
  output out_12
);

  wire undriven, undriven_2, undriven_3, undriven_4;
  wire [3:0] DMA, DSA, UMA, USA;

  or or_1 (out_9, in_1, in_2);
  or or_2 (out_10, in_3, in_4);
  or or_3 (out_11, in_5, in_6);
  or or_4 (out_12, in_7, in_8);
  confr confr_1 (
    .in_2(undriven), .in_3(undriven_2), .in_4(undriven_3), .in_1(undriven_4), .out_5(DMA), .out_6(UMA),
    .out_7(DSA), .out_8(USA));
endmodule

module reset (
  input  in_1,
  input  in_2,
  output out_3
);

  wire and_1_out, xnor_1_out, xnor_2_out, xnor_3_out;
  wire [2:0] adder_1_out, d_ff_3_q, multiplexer_1_out;

  D_Flip_Flop d_ff_1 (.clk(in_1), .D(adder_1_out[2]), .Q(d_ff_3_q[2]));  // open: Qn, preset, en, reset
  D_Flip_Flop d_ff_2 (.clk(in_1), .D(adder_1_out[1]), .Q(d_ff_3_q[1]));  // open: Qn, preset, en, reset
  D_Flip_Flop d_ff_3 (.clk(in_1), .D(adder_1_out[0]), .Q(d_ff_3_q[0]), .preset(in_2));  // open: Qn, en, reset
  Multiplexer #(.width(3), .enable("false")) multiplexer_1 (
    .in0(d_ff_3_q), .in1(3'b111), .out(multiplexer_1_out), .sel(and_1_out));
  xnor xnor_1 (xnor_1_out, d_ff_3_q[2], 1'b0);
  xnor xnor_2 (xnor_2_out, d_ff_3_q[1], 1'b0);
  xnor xnor_3 (xnor_3_out, d_ff_3_q[0], 1'b0);
  Adder #(.width(3)) adder_1 (.a(multiplexer_1_out), .b(3'b001), .out(adder_1_out));  // open: cin, cout
  and and_1 (and_1_out, xnor_1_out, xnor_2_out, xnor_3_out);
  not not_1 (out_3, and_1_out);
endmodule
